// Logisim project 001test_mem.circ as structural Verilog: 1 circuit, main circuit main
module main (
  input  [5:0] in_1,
  input  [5:0] in_2,
  input  [2:0] in_3,
  output [5:0] out_4
);

  wire button_1_out;

  Button button_1 (.out(button_1_out));
  memory_alt_main main_1 (
    .Output(out_4[5]), .out_18(out_4[4]), .out_19(out_4[3]), .out_20(out_4[2]), .out_21(out_4[1]),
    .out_22(out_4[0]), .in_1(in_2[5]), .Alt(in_2[4]), .in_3(in_2[3]), .in_4(in_2[2]), .Address(in_2[1]),
    .in_6(in_2[0]), .Clock(button_1_out), .W(in_3[2]), .R(in_3[1]), .P(in_3[0]), .in_11(in_1[5]),
    .in_12(in_1[4]), .Input(in_1[3]), .in_14(in_1[2]), .in_15(in_1[1]), .in_16(in_1[0]));
endmodule
