// Logisim project 10x upto 9.circ as structural Verilog: 1 circuit, main circuit main
module main (
  input  in_1,
  input  in_2,
  input  in_3,
  input  in_4,
  output out_5,
  output out_6,
  output out_7,
  output out_8,
  output out_9,
  output out_10,
  output out_11
);

  wire main_1_out_13;

  addition_main main_1 (
    .in_1(1'b0), .in_2(1'b0), .in_3(in_1), .in_4(in_2), .in_5(in_3), .in_6(in_4), .in_7(1'b0), .in_8(1'b0),
    .in_9(1'b0), .in_10(1'b0), .in_11(in_1), .in_12(in_2), .out_13(main_1_out_13), .out_14(main_1_out_13),
    .out_15(main_1_out_13), .out_16(out_5), .out_17(out_6), .out_18(out_7), .out_19(out_8));

  assign out_9 = in_3;
  assign out_10 = in_4;
  assign out_11 = 1'b0;
  // also tied to GND on the sheet: main_1_out_13
endmodule
