// Logisim project 10x.circ as structural Verilog: 1 circuit, main circuit main
module main (
  input  in_1,
  input  in_2,
  input  in_3,
  input  in_4,
  input  in_5,
  input  in_6,
  output out_7,
  output out_8,
  output out_9,
  output out_10,
  output out_11,
  output out_12,
  output out_13,
  output out_14,
  output out_15,
  output out_16
);

  addition_main main_1 (
    .in_1(in_1), .in_2(in_2), .in_3(in_3), .in_4(in_4), .in_5(in_5), .in_6(in_6), .in_7(1'b0), .in_8(1'b0),
    .in_9(in_1), .in_10(in_2), .in_11(in_3), .in_12(in_4), .out_13(out_7), .out_14(out_8), .out_15(out_9),
    .out_16(out_10), .out_17(out_11), .out_18(out_12), .out_19(out_13));

  assign out_14 = in_5;
  assign out_15 = in_6;
  assign out_16 = 1'b0;
endmodule
