// Logisim project alt ram.circ as structural Verilog: 1 circuit, main circuit main
module main (
  input  Alt,
  input  in_2,
  input  in_3,
  input  Address,
  input  in_5,
  input  in_6,
  input  Clock,
  input  in_8,
  input  in_9,
  input  in_10,
  input  in_11,
  input  in_12,
  input  in_13,
  input  Write,
  input  Read,
  input  Pass,
  output out_17,
  output out_18,
  output out_19,
  output out_20,
  output out_21,
  output out_22
);

  wire and_1_out, and_2_out, and_3_out, and_4_out, and_5_out, and_6_out, and_7_out, and_8_out, and_9_out,
       and_10_out, and_11_out, and_12_out, not_1_out, not_2_out;
  wire [5:0] controlled_buffer_1_out, ram_1_data;

  RAM #(.addrWidth(3), .dataWidth(6)) ram_1 (
    .addr({Address, in_5, in_6}), .data(ram_1_data), .sel(1'b1), .clk(Clock), .ld(Read), .clr(1'b0));
  assign controlled_buffer_1_out = not_1_out ? ram_1_data : 6'bz;  // Controlled_Buffer controlled_buffer_1
  assign ram_1_data = Write ? {in_8, in_9, in_10, in_11, in_12, in_13} : 6'bz;  // Controlled_Buffer controlled_buffer_2
  not not_1 (not_1_out, Write);
  not not_2 (not_2_out, Pass);
  and and_1 (and_1_out, Alt, Pass);
  and and_2 (and_2_out, controlled_buffer_1_out[5], not_2_out);
  and and_3 (and_3_out, in_2, Pass);
  // OR_Gate or_1 has open pins: in1=and_1_out, in3=and_2_out, out=open
  and and_4 (and_4_out, controlled_buffer_1_out[4], not_2_out);
  and and_5 (and_5_out, in_3, Pass);
  // OR_Gate or_2 has open pins: in1=and_3_out, in3=and_4_out, out=open
  and and_6 (and_6_out, controlled_buffer_1_out[3], not_2_out);
  and and_7 (and_7_out, Address, Pass);
  // OR_Gate or_3 has open pins: in1=and_5_out, in3=and_6_out, out=open
  and and_8 (and_8_out, controlled_buffer_1_out[2], not_2_out);
  and and_9 (and_9_out, in_5, Pass);
  // OR_Gate or_4 has open pins: in1=and_7_out, in3=and_8_out, out=open
  and and_10 (and_10_out, controlled_buffer_1_out[1], not_2_out);
  and and_11 (and_11_out, in_6, Pass);
  // OR_Gate or_5 has open pins: in1=and_9_out, in3=and_10_out, out=open
  and and_12 (and_12_out, controlled_buffer_1_out[0], not_2_out);
  // OR_Gate or_6 has open pins: in1=and_11_out, in3=and_12_out, out=open
endmodule
