// Logisim project bitshifter.circ as structural Verilog: 1 circuit, main circuit main
module main (
  input  [5:0] in_1,
  input  [5:0] in_2,
  output [5:0] out_3
);

  wire not_1_out, or_1_out, or_2_out, or_3_out, or_4_out, or_5_out, or_6_out, or_7_out, or_8_out, or_10_out,
       or_11_out, or_12_out, or_13_out, or_14_out, or_15_out, or_16_out, or_18_out, or_19_out, or_20_out,
       or_21_out, or_22_out, or_23_out, or_24_out, or_25_out, or_26_out, or_28_out, or_29_out, or_30_out,
       or_31_out, or_32_out, or_33_out, or_34_out, or_35_out, or_37_out, or_38_out, or_39_out, or_40_out,
       or_41_out, or_42_out, or_43_out, or_44_out, or_46_out, or_47_out, or_48_out, or_49_out, or_50_out,
       or_51_out, or_52_out, or_53_out;
  wire [2:1] and_38_out;
  wire [4:0] and_9_out, and_10_out;
  wire [5:0] and_23_out, and_45_out;
  wire [5:1] and_68_out;
  wire [5:4] and_13_out, and_14_out, and_27_out, and_48_out, and_61_out;
  wire [5:5] and_36_out, and_49_out;
  wire [9:0] and_21_out;
  wire [9:1] and_15_out, and_17_out, and_19_out;

  not not_1 (not_1_out, in_1[5]);
  and and_1 (and_9_out[4], in_1[4], in_1[5]);
  and and_2 (and_10_out[4], in_1[4], not_1_out);
  and and_3 (and_9_out[3], in_1[3], in_1[5]);
  and and_4 (and_10_out[3], in_1[3], not_1_out);
  and and_5 (and_9_out[2], in_1[2], in_1[5]);
  and and_6 (and_10_out[2], in_1[2], not_1_out);
  and and_7 (and_9_out[1], in_1[1], in_1[5]);
  and and_8 (and_10_out[1], in_1[1], not_1_out);
  and and_9 (and_9_out[0], in_1[0], in_1[5]);
  and and_10 (and_10_out[0], in_1[0], not_1_out);
  and and_11 (and_13_out[5], 1'b0, and_9_out[0]);
  and and_12 (and_14_out[5], in_2[4], and_10_out[0]);
  and and_13 (and_13_out[4], in_2[5], and_9_out[0]);
  and and_14 (and_14_out[4], in_2[3], and_10_out[0]);
  and and_15 (and_15_out[9], in_2[4], and_9_out[0]);
  and and_16 (and_15_out[4], in_2[2], and_10_out[0]);
  and and_17 (and_17_out[9], in_2[3], and_9_out[0]);
  and and_18 (and_17_out[4], in_2[1], and_10_out[0]);
  and and_19 (and_19_out[9], in_2[2], and_9_out[0]);
  and and_20 (and_19_out[4], in_2[0], and_10_out[0]);
  and and_21 (and_21_out[9], in_2[1], and_9_out[0]);
  and and_22 (and_21_out[4], 1'b0, and_10_out[0]);
  and and_23 (and_23_out[5], 1'b0, and_9_out[1]);
  and and_24 (and_23_out[4], 1'b0, and_9_out[1]);
  and and_25 (and_27_out[5], in_2[3], and_10_out[1]);
  and and_26 (and_23_out[3], in_2[5], and_9_out[1]);
  and and_27 (and_27_out[4], in_2[2], and_10_out[1]);
  and and_28 (and_23_out[2], in_2[4], and_9_out[1]);
  and and_29 (and_15_out[3], in_2[1], and_10_out[1]);
  and and_30 (and_23_out[1], in_2[3], and_9_out[1]);
  and and_31 (and_17_out[3], in_2[0], and_10_out[1]);
  and and_32 (and_23_out[0], in_2[2], and_9_out[1]);
  and and_33 (and_19_out[3], 1'b0, and_10_out[1]);
  and and_34 (and_21_out[3], 1'b0, and_10_out[1]);
  or or_1 (or_1_out, and_68_out[5], and_49_out[5]);
  or or_2 (or_2_out, and_23_out[5], and_13_out[5]);
  and and_35 (and_45_out[5], 1'b0, and_9_out[2]);
  and and_36 (and_36_out[5], in_2[2], and_10_out[2]);
  or or_3 (or_3_out, or_1_out, and_36_out[5]);
  or or_4 (or_4_out, and_27_out[5], and_14_out[5]);
  or or_5 (or_5_out, and_61_out[5], and_48_out[5]);
  or or_6 (or_6_out, and_45_out[5], or_2_out);
  and and_37 (and_45_out[4], 1'b0, and_9_out[2]);
  and and_38 (and_38_out[2], in_2[1], and_10_out[2]);
  or or_7 (or_7_out, or_3_out, or_4_out);
  or or_8 (or_8_out, or_5_out, or_6_out);
  and and_39 (and_45_out[3], 1'b0, and_9_out[2]);
  and and_40 (and_15_out[2], in_2[0], and_10_out[2]);
  or or_9 (out_3[5], or_7_out, or_8_out);
  and and_41 (and_45_out[2], in_2[5], and_9_out[2]);
  and and_42 (and_17_out[2], 1'b0, and_10_out[2]);
  and and_43 (and_45_out[1], in_2[4], and_9_out[2]);
  and and_44 (and_19_out[2], 1'b0, and_10_out[2]);
  and and_45 (and_45_out[0], in_2[3], and_9_out[2]);
  and and_46 (and_21_out[2], 1'b0, and_10_out[2]);
  or or_10 (or_10_out, and_68_out[4], and_38_out[1]);
  or or_11 (or_11_out, and_23_out[4], and_13_out[4]);
  and and_47 (and_48_out[5], 1'b0, and_9_out[3]);
  or or_12 (or_12_out, or_10_out, and_38_out[2]);
  or or_13 (or_13_out, and_27_out[4], and_14_out[4]);
  or or_14 (or_14_out, and_61_out[4], and_48_out[4]);
  or or_15 (or_15_out, and_45_out[4], or_11_out);
  and and_48 (and_48_out[4], 1'b0, and_9_out[3]);
  and and_49 (and_49_out[5], in_2[1], and_10_out[3]);
  or or_16 (or_16_out, or_12_out, or_13_out);
  or or_17 (out_3[4], or_16_out, or_18_out);
  or or_18 (or_18_out, or_14_out, or_15_out);
  and and_50 (and_15_out[6], 1'b0, and_9_out[3]);
  and and_51 (and_38_out[1], in_2[0], and_10_out[3]);
  and and_52 (and_17_out[6], 1'b0, and_9_out[3]);
  and and_53 (and_15_out[1], 1'b0, and_10_out[3]);
  and and_54 (and_19_out[6], in_2[5], and_9_out[3]);
  and and_55 (and_17_out[1], 1'b0, and_10_out[3]);
  or or_19 (or_19_out, and_68_out[3], and_15_out[1]);
  or or_20 (or_20_out, and_23_out[3], and_15_out[9]);
  and and_56 (and_21_out[6], in_2[4], and_9_out[3]);
  and and_57 (and_19_out[1], 1'b0, and_10_out[3]);
  or or_21 (or_21_out, or_19_out, and_15_out[2]);
  or or_22 (or_22_out, and_15_out[3], and_15_out[4]);
  or or_23 (or_23_out, and_15_out[5], and_15_out[6]);
  or or_24 (or_24_out, and_45_out[3], or_20_out);
  and and_58 (and_21_out[1], 1'b0, and_10_out[3]);
  or or_25 (or_25_out, or_21_out, or_22_out);
  or or_26 (or_26_out, or_23_out, or_24_out);
  and and_59 (and_61_out[5], 1'b0, and_9_out[4]);
  and and_60 (and_68_out[5], in_2[0], and_10_out[4]);
  or or_27 (out_3[3], or_25_out, or_26_out);
  and and_61 (and_61_out[4], 1'b0, and_9_out[4]);
  and and_62 (and_68_out[4], 1'b0, and_10_out[4]);
  and and_63 (and_15_out[5], 1'b0, and_9_out[4]);
  and and_64 (and_68_out[3], 1'b0, and_10_out[4]);
  or or_28 (or_28_out, and_68_out[2], and_17_out[1]);
  or or_29 (or_29_out, and_23_out[2], and_17_out[9]);
  and and_65 (and_17_out[5], 1'b0, and_9_out[4]);
  and and_66 (and_68_out[2], 1'b0, and_10_out[4]);
  or or_30 (or_30_out, or_28_out, and_17_out[2]);
  or or_31 (or_31_out, and_17_out[3], and_17_out[4]);
  or or_32 (or_32_out, and_17_out[5], and_17_out[6]);
  or or_33 (or_33_out, and_45_out[2], or_29_out);
  and and_67 (and_19_out[5], 1'b0, and_9_out[4]);
  and and_68 (and_68_out[1], 1'b0, and_10_out[4]);
  or or_34 (or_34_out, or_30_out, or_31_out);
  or or_35 (or_35_out, or_32_out, or_33_out);
  and and_69 (and_21_out[5], in_2[5], and_9_out[4]);
  and and_70 (and_21_out[0], 1'b0, and_10_out[4]);
  or or_36 (out_3[2], or_34_out, or_35_out);
  or or_37 (or_37_out, and_68_out[1], and_19_out[1]);
  or or_38 (or_38_out, and_23_out[1], and_19_out[9]);
  or or_39 (or_39_out, or_37_out, and_19_out[2]);
  or or_40 (or_40_out, and_19_out[3], and_19_out[4]);
  or or_41 (or_41_out, and_19_out[5], and_19_out[6]);
  or or_42 (or_42_out, and_45_out[1], or_38_out);
  or or_43 (or_43_out, or_39_out, or_40_out);
  or or_44 (or_44_out, or_41_out, or_42_out);
  or or_45 (out_3[1], or_43_out, or_44_out);
  or or_46 (or_46_out, and_21_out[0], and_21_out[1]);
  or or_47 (or_47_out, and_23_out[0], and_21_out[9]);
  or or_48 (or_48_out, or_46_out, and_21_out[2]);
  or or_49 (or_49_out, and_21_out[3], and_21_out[4]);
  or or_50 (or_50_out, and_21_out[5], and_21_out[6]);
  or or_51 (or_51_out, and_45_out[0], or_47_out);
  or or_52 (or_52_out, or_48_out, or_49_out);
  or or_53 (or_53_out, or_50_out, or_51_out);
  or or_54 (out_3[0], or_52_out, or_53_out);
endmodule
