// Logisim project calculator.circ as structural Verilog: 1 circuit, main circuit main
module main (
  input  in_1,
  input  in_2,
  input  ADD,
  input  SUBTRACT,
  input  MULTIPLY,
  input  DIVIDE
);

  wire button_1_out, button_2_out, button_3_out, button_4_out, button_5_out, button_6_out, button_7_out,
       button_8_out, button_9_out, button_10_out, button_11_out, button_12_out, button_13_out, button_14_out,
       button_15_out, button_16_out, button_17_out, button_18_out, button_19_out, button_20_out,
       button_21_out, button_22_out, main_1_out_13, main_1_out_14, main_1_out_15, main_1_out_16,
       main_1_out_17, main_1_out_18, main_2_out_7, main_2_out_8, main_2_out_9, main_2_out_10, main_2_out_11,
       main_2_out_12, main_2_out_13, main_2_out_14, main_2_out_15, main_2_out_16, main_2_out_17,
       main_2_out_18, main_2_out_19, main_2_out_20, main_2_out_21, main_2_out_22, main_3_out_14,
       main_3_out_15, main_3_out_16, main_3_out_17, main_3_out_18, main_3_out_19, main_4_p13, main_4_p14,
       main_4_p15, main_4_p16, main_4_p17, main_4_p18, main_5_out_14, main_5_out_15, main_5_out_16,
       main_5_out_17, main_5_out_18, main_5_out_19, main_6_out_7, main_6_out_8, main_6_out_9, main_6_out_10,
       main_6_out_11, main_6_out_12, main_6_out_13, main_6_out_14, main_6_out_15, main_6_out_16,
       main_6_out_17, main_6_out_18, main_6_out_19, main_6_out_20, main_6_out_21, main_6_out_22, main_7_p13,
       main_7_p14, main_7_p15, main_7_p16, main_7_p17, main_7_p18, main_8_out_7, main_8_out_8, main_8_out_9,
       main_8_out_10, main_8_out_11, main_8_out_12, main_8_out_13, main_8_out_14, main_8_out_15,
       main_8_out_16, main_8_out_17, main_8_out_18, main_8_out_19, main_8_out_20, main_8_out_21,
       main_8_out_22, main_9_out_14, main_9_out_15, main_9_out_16, main_9_out_17, main_9_out_18,
       main_9_out_19, main_10_out_14, main_10_out_15, main_10_out_16, main_10_out_17, main_10_out_18,
       main_10_out_19, main_11_p1, main_11_p2, main_11_p3, main_11_p4, main_11_p5, main_11_p6,
       main_12_out_19, main_12_out_20, main_12_out_22, main_12_out_23, main_12_out_24, main_12_quotient,
       main_13_out_14, main_13_out_15, main_13_out_16, main_13_out_17, main_13_out_18, main_13_out_19;

  subtraction_main main_1 (
    .in_7(main_7_p13), .in_8(main_7_p14), .in_9(main_7_p15), .in_10(main_7_p16), .in_11(main_7_p17),
    .in_12(main_7_p18), .out_15(main_1_out_15), .out_16(main_1_out_16), .out_17(main_1_out_17),
    .out_18(main_1_out_18), .in_1(main_4_p13), .in_2(main_4_p14), .in_3(main_4_p15), .in_4(main_4_p16),
    .in_5(main_4_p17), .in_6(main_4_p18), .out_13(main_1_out_13), .out_14(main_1_out_14));
  _7_Segment_Display u_7_segment_display_1 (
    .g(main_2_out_11), .f(main_2_out_12), .a(main_2_out_13), .b(main_2_out_14), .e(main_2_out_10),
    .d(main_2_out_9), .c(main_2_out_8), .dp(main_2_out_7));
  _7_Segment_Display u_7_segment_display_2 (
    .g(main_2_out_19), .f(main_2_out_20), .a(main_2_out_21), .b(main_2_out_22), .e(main_2_out_18),
    .d(main_2_out_17), .c(main_2_out_16), .dp(main_2_out_15));
  display_driver_main main_2 (
    .out_7(main_2_out_7), .out_8(main_2_out_8), .out_9(main_2_out_9), .out_10(main_2_out_10),
    .out_11(main_2_out_11), .out_12(main_2_out_12), .out_13(main_2_out_13), .out_14(main_2_out_14),
    .in_1(main_4_p13), .in_2(main_4_p14), .in_3(main_4_p15), .in_4(main_4_p16), .in_5(main_4_p17),
    .in_6(main_4_p18), .out_15(main_2_out_15), .out_16(main_2_out_16), .out_17(main_2_out_17),
    .out_18(main_2_out_18), .out_19(main_2_out_19), .out_20(main_2_out_20), .out_21(main_2_out_21),
    .out_22(main_2_out_22));
  Button button_1 (.out(button_1_out));
  Button button_2 (.out(button_2_out));
  Button button_3 (.out(button_3_out));
  Button button_4 (.out(button_4_out));
  Button button_5 (.out(button_5_out));
  Button button_6 (.out(button_6_out));
  Button button_7 (.out(button_7_out));
  Button button_8 (.out(button_8_out));
  Button button_9 (.out(button_9_out));
  Button button_10 (.out(button_10_out));
  Button button_11 (.out(button_11_out));
  addition_main main_3 (
    .in_1(main_4_p13), .in_2(main_4_p14), .in_3(main_4_p15), .in_4(main_4_p16), .in_5(main_4_p17),
    .in_6(main_4_p18), .in_7(main_7_p13), .in_8(main_7_p14), .in_9(main_7_p15), .in_10(main_7_p16),
    .in_11(main_7_p17), .in_12(main_7_p18), .out_14(main_3_out_14), .out_15(main_3_out_15),
    .out_16(main_3_out_16), .out_17(main_3_out_17), .out_18(main_3_out_18), .out_19(main_3_out_19));  // open: out_13
  // numpad_main main_4: pin names not known; wires that end beside it: in_1, button_1_out, button_2_out, button_3_out, button_4_out, button_5_out, button_6_out, button_7_out, button_8_out, button_9_out, button_10_out, button_11_out, main_4_p13, main_4_p14, main_4_p15, main_4_p16, main_4_p17, main_4_p18
  output_selector_main main_5 (
    .in_7(SUBTRACT), .in_1(1'b0), .out_14(main_5_out_14), .in_2(1'b0), .out_15(main_5_out_15), .in_3(1'b0),
    .out_16(main_5_out_16), .in_4(1'b0), .out_17(main_5_out_17), .in_5(1'b0), .out_18(main_5_out_18),
    .in_6(1'b0), .out_19(main_5_out_19), .in_8(main_1_out_15), .in_9(main_1_out_16), .in_10(main_1_out_17),
    .in_11(main_1_out_18), .in_12(main_1_out_13), .in_13(main_1_out_14));
  _7_Segment_Display u_7_segment_display_3 (
    .g(main_6_out_11), .f(main_6_out_12), .a(main_6_out_13), .b(main_6_out_14), .e(main_6_out_10),
    .d(main_6_out_9), .c(main_6_out_8), .dp(main_6_out_7));
  Button button_12 (.out(button_12_out));
  Button button_13 (.out(button_13_out));
  Button button_14 (.out(button_14_out));
  Button button_15 (.out(button_15_out));
  Button button_16 (.out(button_16_out));
  Button button_17 (.out(button_17_out));
  Button button_18 (.out(button_18_out));
  Button button_19 (.out(button_19_out));
  Button button_20 (.out(button_20_out));
  Button button_21 (.out(button_21_out));
  Button button_22 (.out(button_22_out));
  _7_Segment_Display u_7_segment_display_4 (
    .g(main_6_out_19), .f(main_6_out_20), .a(main_6_out_21), .b(main_6_out_22), .e(main_6_out_18),
    .d(main_6_out_17), .c(main_6_out_16), .dp(main_6_out_15));
  display_driver_main main_6 (
    .out_7(main_6_out_7), .out_8(main_6_out_8), .out_9(main_6_out_9), .out_10(main_6_out_10),
    .out_11(main_6_out_11), .out_12(main_6_out_12), .out_13(main_6_out_13), .out_14(main_6_out_14),
    .in_1(main_7_p13), .in_2(main_7_p14), .in_3(main_7_p15), .in_4(main_7_p16), .in_5(main_7_p17),
    .in_6(main_7_p18), .out_15(main_6_out_15), .out_16(main_6_out_16), .out_17(main_6_out_17),
    .out_18(main_6_out_18), .out_19(main_6_out_19), .out_20(main_6_out_20), .out_21(main_6_out_21),
    .out_22(main_6_out_22));
  // numpad_main main_7: pin names not known; wires that end beside it: in_2, button_12_out, button_13_out, button_14_out, button_15_out, button_16_out, button_17_out, button_18_out, button_19_out, button_20_out, button_21_out, button_22_out, main_7_p13, main_7_p14, main_7_p15, main_7_p16, main_7_p17, main_7_p18
  _7_Segment_Display u_7_segment_display_5 (
    .g(main_8_out_11), .f(main_8_out_12), .a(main_8_out_13), .b(main_8_out_14), .e(main_8_out_10),
    .d(main_8_out_9), .c(main_8_out_8), .dp(main_8_out_7));
  display_driver_main main_8 (
    .out_7(main_8_out_7), .out_8(main_8_out_8), .out_9(main_8_out_9), .out_10(main_8_out_10),
    .out_11(main_8_out_11), .out_12(main_8_out_12), .out_13(main_8_out_13), .out_14(main_8_out_14),
    .in_1(main_9_out_14), .in_2(main_9_out_15), .in_3(main_9_out_16), .in_4(main_9_out_17),
    .in_5(main_9_out_18), .in_6(main_9_out_19), .out_15(main_8_out_15), .out_16(main_8_out_16),
    .out_17(main_8_out_17), .out_18(main_8_out_18), .out_19(main_8_out_19), .out_20(main_8_out_20),
    .out_21(main_8_out_21), .out_22(main_8_out_22));
  output_selector_main main_9 (
    .in_7(ADD), .in_1(main_13_out_14), .out_14(main_9_out_14), .in_2(main_13_out_15), .out_15(main_9_out_15),
    .in_3(main_13_out_16), .out_16(main_9_out_16), .in_4(main_13_out_17), .out_17(main_9_out_17),
    .in_5(main_13_out_18), .out_18(main_9_out_18), .in_6(main_13_out_19), .out_19(main_9_out_19),
    .in_8(main_3_out_14), .in_9(main_3_out_15), .in_10(main_3_out_16), .in_11(main_3_out_17),
    .in_12(main_3_out_18), .in_13(main_3_out_19));
  output_selector_main main_10 (
    .in_7(DIVIDE), .in_1(main_5_out_14), .out_14(main_10_out_14), .in_2(main_5_out_15),
    .out_15(main_10_out_15), .in_3(main_5_out_16), .out_16(main_10_out_16), .in_4(main_5_out_17),
    .out_17(main_10_out_17), .in_5(main_5_out_18), .out_18(main_10_out_18), .in_6(main_5_out_19),
    .out_19(main_10_out_19), .in_8(main_12_out_19), .in_9(main_12_out_20), .in_10(main_12_quotient),
    .in_11(main_12_out_22), .in_12(main_12_out_23), .in_13(main_12_out_24));
  _7_Segment_Display u_7_segment_display_6 (
    .g(main_8_out_19), .f(main_8_out_20), .a(main_8_out_21), .b(main_8_out_22), .e(main_8_out_18),
    .d(main_8_out_17), .c(main_8_out_16), .dp(main_8_out_15));
  // multiplication_main main_11: pin names not known; wires that end beside it: main_11_p1, main_11_p2, main_11_p3, main_11_p4, main_11_p5, main_11_p6
  division_main main_12 (
    .out_19(main_12_out_19), .out_20(main_12_out_20), .Quotient(main_12_quotient), .out_22(main_12_out_22),
    .out_23(main_12_out_23), .out_24(main_12_out_24), .in_1(main_7_p13), .in_2(main_7_p14),
    .in_3(main_7_p15), .Divisor(main_7_p16), .in_5(main_7_p17), .in_6(main_7_p18), .in_7(main_4_p13),
    .in_8(main_4_p14), .Dividend(main_4_p15), .in_10(main_4_p16), .in_11(main_4_p17), .in_12(main_4_p18));  // open: out_13, out_14, Remainder, out_16, out_17, out_18
  output_selector_main main_13 (
    .in_7(MULTIPLY), .in_1(main_10_out_14), .out_14(main_13_out_14), .in_2(main_10_out_15),
    .out_15(main_13_out_15), .in_3(main_10_out_16), .out_16(main_13_out_16), .in_4(main_10_out_17),
    .out_17(main_13_out_17), .in_5(main_10_out_18), .out_18(main_13_out_18), .in_6(main_10_out_19),
    .out_19(main_13_out_19), .in_8(main_11_p1), .in_9(main_11_p2), .in_10(main_11_p3), .in_11(main_11_p4),
    .in_12(main_11_p5), .in_13(main_11_p6));
endmodule
