// Logisim project counter.circ as structural Verilog: 1 circuit, main circuit main
module main (
);

  wire and_1_out, and_2_out, and_3_out, and_4_out, and_5_out, and_6_out, and_7_out, and_8_out, and_9_out,
       and_10_out, and_11_out, button_1_out, button_2_out, nand_1_out, nand_2_out, nand_3_out, nand_4_out,
       nand_5_out, nand_6_out, nand_7_out, nand_8_out, nand_9_out, nand_10_out, nand_11_out, nand_12_out,
       nand_13_out, nand_14_out, nand_15_out, nand_16_out, nand_17_out, nand_18_out, nand_19_out,
       nand_20_out, nand_21_out, nand_22_out, nand_23_out, nand_24_out, nand_25_out, nand_26_out,
       nand_27_out, nand_28_out, nand_29_out, nand_30_out, nand_31_out, nand_32_out, nand_33_out,
       nand_34_out, nand_35_out, nand_36_out, nand_37_out, nand_38_out, nand_39_out, nand_40_out,
       nand_41_out, nand_42_out, nand_43_out, nand_44_out, nand_45_out, nand_46_out, nand_47_out,
       nand_48_out, not_1_out, not_2_out, not_3_out, not_4_out, not_5_out, not_6_out, not_7_out, not_8_out,
       not_9_out, not_10_out, not_11_out, not_12_out, not_13_out, or_1_out, xor_1_out, xor_2_out, xor_3_out,
       xor_4_out, xor_5_out, xor_6_out;

  Button button_1 (.out(button_1_out));
  Button button_2 (.out(button_2_out));
  not not_1 (not_1_out, button_2_out);
  LED led_1 (.in(nand_48_out));
  and and_1 (and_1_out, nand_48_out, button_2_out);
  LED led_2 (.in(nand_46_out));
  LED led_3 (.in(nand_44_out));
  and and_2 (and_2_out, nand_46_out, button_2_out);
  LED led_4 (.in(nand_42_out));
  and and_3 (and_3_out, nand_44_out, button_2_out);
  and and_4 (and_4_out, nand_42_out, button_2_out);
  LED led_5 (.in(and_1_out));
  LED led_6 (.in(nand_40_out));
  and and_5 (and_5_out, nand_40_out, button_2_out);
  LED led_7 (.in(and_3_out));
  LED led_8 (.in(and_2_out));
  LED led_9 (.in(nand_38_out));
  LED led_10 (.in(and_5_out));
  LED led_11 (.in(and_4_out));
  xor xor_1 (xor_1_out, and_2_out, and_9_out);
  and and_6 (and_6_out, and_2_out, and_9_out);
  xor xor_2 (xor_2_out, and_1_out, and_6_out);
  and and_7 (and_7_out, nand_38_out, button_2_out);
  LED led_12 (.in(and_7_out));
  xor xor_3 (xor_3_out, and_4_out, and_10_out);
  and and_8 (and_8_out, and_4_out, and_10_out);
  xor xor_4 (xor_4_out, and_3_out, and_8_out);
  and and_9 (and_9_out, and_3_out, and_8_out);
  xor xor_5 (xor_5_out, and_5_out, and_11_out);
  and and_10 (and_10_out, and_5_out, and_11_out);
  xor xor_6 (xor_6_out, and_7_out, button_2_out);
  and and_11 (and_11_out, and_7_out, button_2_out);
  or or_1 (or_1_out, button_1_out, button_2_out);
  not not_2 (not_2_out, xor_6_out);
  not not_3 (not_3_out, xor_5_out);
  not not_4 (not_4_out, xor_3_out);
  not not_5 (not_5_out, xor_4_out);
  not not_6 (not_6_out, xor_1_out);
  not not_7 (not_7_out, xor_2_out);
  nand nand_1 (nand_1_out, not_2_out, or_1_out);
  nand nand_2 (nand_2_out, or_1_out, xor_6_out);
  nand nand_3 (nand_3_out, not_3_out, or_1_out);
  nand nand_4 (nand_4_out, or_1_out, xor_5_out);
  nand nand_5 (nand_5_out, not_4_out, or_1_out);
  nand nand_6 (nand_6_out, or_1_out, xor_3_out);
  nand nand_7 (nand_7_out, not_5_out, or_1_out);
  nand nand_8 (nand_8_out, or_1_out, xor_4_out);
  nand nand_9 (nand_9_out, not_6_out, or_1_out);
  nand nand_10 (nand_10_out, or_1_out, xor_1_out);
  nand nand_11 (nand_11_out, not_7_out, or_1_out);
  nand nand_12 (nand_12_out, or_1_out, xor_2_out);
  nand nand_13 (nand_13_out, nand_1_out, nand_14_out);
  nand nand_14 (nand_14_out, nand_13_out, nand_2_out);
  nand nand_15 (nand_15_out, nand_3_out, nand_16_out);
  nand nand_16 (nand_16_out, nand_15_out, nand_4_out);
  nand nand_17 (nand_17_out, nand_5_out, nand_18_out);
  nand nand_18 (nand_18_out, nand_17_out, nand_6_out);
  nand nand_19 (nand_19_out, nand_7_out, nand_20_out);
  nand nand_20 (nand_20_out, nand_19_out, nand_8_out);
  nand nand_21 (nand_21_out, nand_9_out, nand_22_out);
  nand nand_22 (nand_22_out, nand_21_out, nand_10_out);
  nand nand_23 (nand_23_out, nand_11_out, nand_24_out);
  nand nand_24 (nand_24_out, nand_23_out, nand_12_out);
  LED led_13 (.in(nand_14_out));
  LED led_14 (.in(nand_16_out));
  LED led_15 (.in(nand_18_out));
  LED led_16 (.in(nand_20_out));
  LED led_17 (.in(nand_22_out));
  LED led_18 (.in(nand_24_out));
  not not_8 (not_8_out, nand_14_out);
  not not_9 (not_9_out, nand_16_out);
  not not_10 (not_10_out, nand_18_out);
  not not_11 (not_11_out, nand_20_out);
  not not_12 (not_12_out, nand_22_out);
  not not_13 (not_13_out, nand_24_out);
  nand nand_25 (nand_25_out, not_8_out, not_1_out);
  nand nand_26 (nand_26_out, not_1_out, nand_14_out);
  nand nand_27 (nand_27_out, not_9_out, not_1_out);
  nand nand_28 (nand_28_out, not_1_out, nand_16_out);
  nand nand_29 (nand_29_out, not_10_out, not_1_out);
  nand nand_30 (nand_30_out, not_1_out, nand_18_out);
  nand nand_31 (nand_31_out, not_11_out, not_1_out);
  nand nand_32 (nand_32_out, not_1_out, nand_20_out);
  nand nand_33 (nand_33_out, not_12_out, not_1_out);
  nand nand_34 (nand_34_out, not_1_out, nand_22_out);
  nand nand_35 (nand_35_out, not_13_out, not_1_out);
  nand nand_36 (nand_36_out, not_1_out, nand_24_out);
  nand nand_37 (nand_37_out, nand_25_out, nand_38_out);
  nand nand_38 (nand_38_out, nand_37_out, nand_26_out);
  nand nand_39 (nand_39_out, nand_27_out, nand_40_out);
  nand nand_40 (nand_40_out, nand_39_out, nand_28_out);
  nand nand_41 (nand_41_out, nand_29_out, nand_42_out);
  nand nand_42 (nand_42_out, nand_41_out, nand_30_out);
  nand nand_43 (nand_43_out, nand_31_out, nand_44_out);
  nand nand_44 (nand_44_out, nand_43_out, nand_32_out);
  nand nand_45 (nand_45_out, nand_33_out, nand_46_out);
  nand nand_46 (nand_46_out, nand_45_out, nand_34_out);
  nand nand_47 (nand_47_out, nand_35_out, nand_48_out);
  nand nand_48 (nand_48_out, nand_47_out, nand_36_out);

  // Notes on the sheet:
  //   Initialise/Reset Counter
  //   Pulse for counter
  //   Counted value
endmodule
