// Logisim project counter_with_memory.circ as structural Verilog: 1 circuit, main circuit main
module main (
  input  in_1
);

  wire and_1_out, and_2_out, and_3_out, and_4_out, and_5_out, and_6_out, and_7_out, and_8_out, and_9_out,
       and_10_out, and_11_out, and_12_out, button_1_out, nand_1_out, nand_2_out, nand_3_out, nand_4_out,
       nand_5_out, nand_6_out, nand_7_out, nand_8_out, nand_9_out, nand_10_out, nand_11_out, nand_12_out,
       nand_13_out, nand_14_out, nand_15_out, nand_16_out, nand_17_out, nand_18_out, nand_19_out,
       nand_20_out, nand_21_out, nand_22_out, nand_23_out, nand_24_out, not_1_out, not_2_out, not_3_out,
       not_4_out, not_5_out, not_6_out, xor_1_out, xor_2_out, xor_3_out, xor_4_out, xor_5_out, xor_6_out;

  Button button_1 (.out(button_1_out));
  and and_1 (and_1_out, nand_24_out, in_1);
  and and_2 (and_2_out, nand_22_out, in_1);
  LED led_1 (.in(nand_24_out));
  LED led_2 (.in(nand_22_out));
  and and_3 (and_3_out, nand_20_out, in_1);
  LED led_3 (.in(and_1_out));
  LED led_4 (.in(nand_18_out));
  LED led_5 (.in(nand_20_out));
  and and_4 (and_4_out, nand_18_out, in_1);
  LED led_6 (.in(and_2_out));
  LED led_7 (.in(and_3_out));
  LED led_8 (.in(nand_16_out));
  LED led_9 (.in(nand_14_out));
  and and_5 (and_5_out, nand_16_out, in_1);
  LED led_10 (.in(and_5_out));
  LED led_11 (.in(and_4_out));
  xor xor_1 (xor_1_out, and_2_out, and_10_out);
  and and_6 (and_6_out, and_2_out, and_10_out);
  xor xor_2 (xor_2_out, and_1_out, and_6_out);
  and and_7 (and_7_out, and_1_out, and_6_out);
  and and_8 (and_8_out, nand_14_out, in_1);
  LED led_12 (.in(and_8_out));
  xor xor_3 (xor_3_out, and_4_out, and_12_out);
  and and_9 (and_9_out, and_4_out, and_12_out);
  xor xor_4 (xor_4_out, and_3_out, and_9_out);
  and and_10 (and_10_out, and_3_out, and_9_out);
  xor xor_5 (xor_5_out, and_8_out, button_1_out);
  and and_11 (and_11_out, and_8_out, button_1_out);
  xor xor_6 (xor_6_out, and_5_out, and_11_out);
  and and_12 (and_12_out, and_5_out, and_11_out);
  LED led_13 (.in(and_7_out));
  not not_1 (not_1_out, xor_5_out);
  not not_2 (not_2_out, xor_6_out);
  not not_3 (not_3_out, xor_3_out);
  not not_4 (not_4_out, xor_4_out);
  not not_5 (not_5_out, xor_1_out);
  not not_6 (not_6_out, xor_2_out);
  nand nand_1 (nand_1_out, not_1_out, button_1_out);
  nand nand_2 (nand_2_out, button_1_out, xor_5_out);
  nand nand_3 (nand_3_out, not_2_out, button_1_out);
  nand nand_4 (nand_4_out, button_1_out, xor_6_out);
  nand nand_5 (nand_5_out, not_3_out, button_1_out);
  nand nand_6 (nand_6_out, button_1_out, xor_3_out);
  nand nand_7 (nand_7_out, not_4_out, button_1_out);
  nand nand_8 (nand_8_out, button_1_out, xor_4_out);
  nand nand_9 (nand_9_out, not_5_out, button_1_out);
  nand nand_10 (nand_10_out, button_1_out, xor_1_out);
  nand nand_11 (nand_11_out, not_6_out, button_1_out);
  nand nand_12 (nand_12_out, button_1_out, xor_2_out);
  nand nand_13 (nand_13_out, nand_1_out, nand_14_out);
  nand nand_14 (nand_14_out, nand_13_out, nand_2_out);
  nand nand_15 (nand_15_out, nand_3_out, nand_16_out);
  nand nand_16 (nand_16_out, nand_15_out, nand_4_out);
  nand nand_17 (nand_17_out, nand_5_out, nand_18_out);
  nand nand_18 (nand_18_out, nand_17_out, nand_6_out);
  nand nand_19 (nand_19_out, nand_7_out, nand_20_out);
  nand nand_20 (nand_20_out, nand_19_out, nand_8_out);
  nand nand_21 (nand_21_out, nand_9_out, nand_22_out);
  nand nand_22 (nand_22_out, nand_21_out, nand_10_out);
  nand nand_23 (nand_23_out, nand_11_out, nand_24_out);
  nand nand_24 (nand_24_out, nand_23_out, nand_12_out);
endmodule
