// Logisim project display driver.circ as structural Verilog: 1 circuit, main circuit main
module main (
  input  in_1,
  input  in_2,
  input  in_3,
  input  in_4,
  input  in_5,
  input  in_6,
  output out_7,
  output out_8,
  output out_9,
  output out_10,
  output out_11,
  output out_12,
  output out_13,
  output out_14,
  output out_15,
  output out_16,
  output out_17,
  output out_18,
  output out_19,
  output out_20,
  output out_21,
  output out_22
);

  wire main_2_out_8, main_2_out_9, main_2_out_10, main_2_out_12, main_2_out_13, main_2_quotient,
       main_2_remainder;

  seven_segment_display_main main_1 (
    .out_9(out_10), .out_10(out_9), .out_11(out_8), .out_12(out_7), .in_1(1'b0), .in_2(main_2_quotient),
    .in_3(main_2_out_12), .in_4(main_2_out_13), .out_5(out_11), .out_6(out_12), .out_7(out_13), .out_8(out_14));
  bin_to_dec_main main_2 (
    .Quotient(main_2_quotient), .out_12(main_2_out_12), .out_13(main_2_out_13), .in_1(in_1), .in_2(in_2),
    .Dividend(in_3), .in_4(in_4), .in_5(in_5), .in_6(in_6), .out_8(main_2_out_8), .out_9(main_2_out_9),
    .out_10(main_2_out_10), .Remainder(main_2_remainder));
  seven_segment_display_main main_3 (
    .out_9(out_18), .out_10(out_17), .out_11(out_16), .out_12(out_15), .in_1(main_2_remainder),
    .in_2(main_2_out_8), .in_3(main_2_out_9), .in_4(main_2_out_10), .out_5(out_19), .out_6(out_20),
    .out_7(out_21), .out_8(out_22));
endmodule
