// Logisim project display driver2.circ as structural Verilog: 1 circuit, main circuit main
module main (
  input  [5:0] in_1,
  output [15:0] out_2
);

  wire main_1_p6, main_1_p7, main_1_p8, main_1_p17, main_1_p18, main_1_p19, main_1_p20, main_1_p21,
       main_1_p22, main_1_p23, main_1_p24, main_1_p25, main_1_p26, main_1_p27, main_1_p28, main_1_p29,
       main_1_p30, main_1_p31, main_1_p32, main_1_p33, main_1_p34, main_1_p35, main_1_p36, main_1_p37,
       main_1_p38, main_1_p39, main_1_p40, main_1_p41, main_1_p42, main_1_p43, main_1_p44, main_1_p45,
       main_1_p46, main_1_p47, main_1_p48, main_1_p49, main_1_p50, main_1_p51, main_1_p52, main_1_p53,
       main_1_p54, main_1_p55, main_1_p56, main_1_p57, main_1_p58, main_1_p59, main_1_p60, main_1_p61,
       main_1_p62, main_1_p63, main_1_p64, main_1_p65, main_1_p66, main_1_p67, main_1_p68, main_1_p69,
       main_1_p70, main_1_p71, main_1_p72, main_1_p73, main_1_p74, main_1_p75, main_1_p76, main_1_p77,
       main_1_p78, main_1_p79, main_1_p80, main_1_p81, main_1_p82, main_1_p83, main_1_p84, main_1_p85,
       main_1_p86, main_1_p87, main_1_p88, main_1_p89, main_1_p90, main_1_p91, main_1_p92, main_1_p93,
       main_1_p94, main_1_p95, main_1_p96, main_1_p97, main_1_p98, main_1_p99, main_1_p100, main_1_p101,
       main_1_p102, main_1_p103, main_1_p104, main_1_p105, main_1_p106, main_1_p107, main_1_p108,
       main_1_p109, main_1_p110, main_1_p111, main_1_p112, main_1_p113, main_1_p114, main_1_p115,
       main_1_p116, main_1_p117, main_1_p118, main_1_p119, main_1_p120, main_1_p121, main_1_p122,
       main_1_p123, main_1_p124;

  // seven_segment_display_main main_1: pin names not known; wires that end beside it: out_2[5], out_2[13], out_2[4], out_2[12], 1'b0, main_1_p6, main_1_p7, main_1_p8, out_2[3], out_2[11], out_2[2], out_2[10], out_2[1], out_2[9], out_2[0], out_2[8], main_1_p17, main_1_p18, main_1_p19, main_1_p20, main_1_p21, main_1_p22, main_1_p23, main_1_p24, main_1_p25, main_1_p26, main_1_p27, main_1_p28, main_1_p29, main_1_p30, main_1_p31, main_1_p32, main_1_p33, main_1_p34, main_1_p35, main_1_p36, main_1_p37, main_1_p38, main_1_p39, main_1_p40, main_1_p41, main_1_p42, main_1_p43, main_1_p44, main_1_p45, main_1_p46, main_1_p47, main_1_p48, main_1_p49, main_1_p50, main_1_p51, main_1_p52, main_1_p53, main_1_p54, main_1_p55, main_1_p56, main_1_p57, main_1_p58, main_1_p59, main_1_p60, main_1_p61, main_1_p62, main_1_p63, main_1_p64, main_1_p65, main_1_p66, main_1_p67, main_1_p68, main_1_p69, main_1_p70, main_1_p71, main_1_p72, main_1_p73, main_1_p74, main_1_p75, main_1_p76, main_1_p77, main_1_p78, main_1_p79, main_1_p80, main_1_p81, main_1_p82, main_1_p83, main_1_p84, main_1_p85, main_1_p86, main_1_p87, main_1_p88, main_1_p89, main_1_p90, main_1_p91, main_1_p92, main_1_p93, main_1_p94, main_1_p95, main_1_p96, main_1_p97, main_1_p98, main_1_p99, main_1_p100, main_1_p101, main_1_p102, main_1_p103, main_1_p104, main_1_p105, main_1_p106, main_1_p107, main_1_p108, main_1_p109, main_1_p110, main_1_p111, main_1_p112, main_1_p113, main_1_p114, main_1_p115, main_1_p116, main_1_p117, main_1_p118, main_1_p119, main_1_p120, main_1_p121, main_1_p122, main_1_p123, main_1_p124
  bin_to_dec_main main_2 (
    .Quotient(main_1_p6), .out_12(main_1_p7), .out_13(main_1_p8), .in_1(in_1[5]), .in_2(in_1[4]),
    .Dividend(in_1[3]), .in_4(in_1[2]), .in_5(in_1[1]), .in_6(in_1[0]), .out_8(main_1_p21),
    .out_9(main_1_p24), .out_10(main_1_p27), .Remainder(main_1_p18));
  // seven_segment_display_main main_3: pin names not known; wires that end beside it: out_2[1], out_2[9], out_2[0], out_2[8], main_1_p17, main_1_p18, main_1_p19, main_1_p20, main_1_p21, main_1_p22, main_1_p23, main_1_p24, main_1_p25, main_1_p26, main_1_p27, main_1_p28, main_1_p29, main_1_p30, main_1_p31, main_1_p32, main_1_p33, main_1_p34, main_1_p35, main_1_p36, main_1_p37, main_1_p38, main_1_p39, main_1_p40, main_1_p41, main_1_p42, main_1_p43, main_1_p44, main_1_p45, main_1_p46, main_1_p47, main_1_p48, main_1_p49, main_1_p50, main_1_p51, main_1_p52, main_1_p53, main_1_p54, main_1_p55, main_1_p56, main_1_p57, main_1_p58, main_1_p59, main_1_p60, main_1_p61, main_1_p62, main_1_p63, main_1_p64, main_1_p65, main_1_p66, main_1_p67, main_1_p68, main_1_p69, main_1_p70, main_1_p71, main_1_p72, main_1_p73, main_1_p74, main_1_p75, main_1_p76, main_1_p77, main_1_p78, main_1_p79, main_1_p80, main_1_p81, main_1_p82, main_1_p83, main_1_p84, main_1_p85, main_1_p86, main_1_p87, main_1_p88, main_1_p89, main_1_p90, main_1_p91, main_1_p92, main_1_p93, main_1_p94, main_1_p95, main_1_p96, main_1_p97, main_1_p98, main_1_p99, main_1_p100, main_1_p101, main_1_p102, main_1_p103, main_1_p104, main_1_p105, main_1_p106, main_1_p107, main_1_p108, main_1_p109, main_1_p110, main_1_p111, main_1_p112, main_1_p113, main_1_p114, main_1_p115, main_1_p116, main_1_p117, main_1_p118, main_1_p119, main_1_p120, main_1_p121, main_1_p122, main_1_p123, main_1_p124
endmodule
