// Logisim project equality check.circ as structural Verilog: 1 circuit, main circuit main
module main (
  input  in_1,
  input  in_2,
  input  Number_A,
  input  in_4,
  input  in_5,
  input  in_6,
  input  in_7,
  input  in_8,
  input  in_9,
  input  in_10,
  input  in_11,
  input  in_12
);

  wire and_1_out, and_2_out, and_3_out, and_4_out, and_5_out, xnor_1_out, xnor_2_out, xnor_3_out, xnor_4_out,
       xnor_5_out, xnor_6_out;

  LED led_1 (.in(and_5_out));
  xnor xnor_1 (xnor_1_out, in_12, in_6);
  xnor xnor_2 (xnor_2_out, in_11, in_5);
  xnor xnor_3 (xnor_3_out, in_10, in_4);
  xnor xnor_4 (xnor_4_out, in_9, Number_A);
  xnor xnor_5 (xnor_5_out, in_8, in_2);
  xnor xnor_6 (xnor_6_out, in_7, in_1);
  and and_1 (and_1_out, xnor_1_out, xnor_2_out);
  and and_2 (and_2_out, and_1_out, xnor_3_out);
  and and_3 (and_3_out, and_2_out, xnor_4_out);
  and and_4 (and_4_out, and_3_out, xnor_5_out);
  and and_5 (and_5_out, and_4_out, xnor_6_out);

  // Notes on the sheet:
  //   Equality Check
  //   Number B
endmodule
