// Logisim project gated d latch.circ as structural Verilog: 1 circuit, main circuit main
module main (
  input  Enable,
  input  in_2,
  input  in_3,
  input  in_4,
  input  in_5,
  input  in_6,
  input  in_7
);

  wire and_1_out, and_2_out, and_3_out, and_4_out, and_5_out, and_6_out, button_1_out, nand_1_out,
       nand_2_out, nand_3_out, nand_4_out, nand_5_out, nand_6_out, nand_7_out, nand_8_out, nand_9_out,
       nand_10_out, nand_11_out, nand_12_out, nand_13_out, nand_14_out, nand_15_out, nand_16_out,
       nand_17_out, nand_18_out, nand_19_out, nand_20_out, nand_21_out, nand_22_out, nand_23_out,
       nand_24_out, not_1_out, not_2_out, not_3_out, not_4_out, not_5_out, not_6_out, not_7_out, or_1_out;

  Button button_1 (.out(button_1_out));
  not not_1 (not_1_out, button_1_out);
  and and_1 (and_1_out, not_1_out, in_7);
  and and_2 (and_2_out, not_1_out, in_6);
  and and_3 (and_3_out, not_1_out, in_5);
  and and_4 (and_4_out, not_1_out, in_4);
  and and_5 (and_5_out, not_1_out, in_3);
  and and_6 (and_6_out, not_1_out, in_2);
  not not_2 (not_2_out, and_1_out);
  not not_3 (not_3_out, and_2_out);
  not not_4 (not_4_out, and_3_out);
  not not_5 (not_5_out, and_4_out);
  not not_6 (not_6_out, and_5_out);
  not not_7 (not_7_out, and_6_out);
  or or_1 (or_1_out, Enable, button_1_out);
  nand nand_1 (nand_1_out, not_2_out, or_1_out);
  nand nand_2 (nand_2_out, or_1_out, and_1_out);
  nand nand_3 (nand_3_out, not_3_out, or_1_out);
  nand nand_4 (nand_4_out, or_1_out, and_2_out);
  nand nand_5 (nand_5_out, not_4_out, or_1_out);
  nand nand_6 (nand_6_out, or_1_out, and_3_out);
  nand nand_7 (nand_7_out, not_5_out, or_1_out);
  nand nand_8 (nand_8_out, or_1_out, and_4_out);
  nand nand_9 (nand_9_out, not_6_out, or_1_out);
  nand nand_10 (nand_10_out, or_1_out, and_5_out);
  nand nand_11 (nand_11_out, not_7_out, or_1_out);
  nand nand_12 (nand_12_out, or_1_out, and_6_out);
  nand nand_13 (nand_13_out, nand_1_out, nand_14_out);
  nand nand_14 (nand_14_out, nand_13_out, nand_2_out);
  nand nand_15 (nand_15_out, nand_3_out, nand_16_out);
  nand nand_16 (nand_16_out, nand_15_out, nand_4_out);
  nand nand_17 (nand_17_out, nand_5_out, nand_18_out);
  nand nand_18 (nand_18_out, nand_17_out, nand_6_out);
  nand nand_19 (nand_19_out, nand_7_out, nand_20_out);
  nand nand_20 (nand_20_out, nand_19_out, nand_8_out);
  nand nand_21 (nand_21_out, nand_9_out, nand_22_out);
  nand nand_22 (nand_22_out, nand_21_out, nand_10_out);
  nand nand_23 (nand_23_out, nand_11_out, nand_24_out);
  nand nand_24 (nand_24_out, nand_23_out, nand_12_out);
  LED led_1 (.in(nand_24_out));
  LED led_2 (.in(nand_22_out));
  LED led_3 (.in(nand_20_out));
  LED led_4 (.in(nand_18_out));
  LED led_5 (.in(nand_16_out));
  LED led_6 (.in(nand_14_out));

  // Notes on the sheet:
  //   Initialise / Reset
endmodule
