// Logisim project input selector.circ as structural Verilog: 1 circuit, main circuit main
module main (
  input  [5:0] in_1,
  input  [5:0] in_2,
  input  [5:0] in_3,
  input  in_4,
  input  [5:0] in_5,
  input  [5:0] in_6,
  input  [5:0] in_7,
  output [5:0] out_8,
  output [5:0] out_9,
  output [5:0] out_10
);

  wire and_1_out, and_2_out, and_3_out, and_4_out, and_5_out, and_6_out, and_7_out, and_8_out, and_9_out,
       and_10_out, and_11_out, and_12_out, and_13_out, and_14_out, and_15_out, and_16_out, and_17_out,
       and_18_out, and_19_out, and_20_out, and_21_out, and_22_out, and_23_out, and_24_out, and_25_out,
       and_26_out, and_27_out, and_28_out, and_29_out, and_30_out, and_31_out, and_32_out, and_33_out,
       and_34_out, and_35_out, and_36_out, not_1_out;

  not not_1 (not_1_out, in_4);
  and and_1 (and_1_out, in_1[5], not_1_out);
  and and_2 (and_2_out, in_4, in_5[5]);
  or or_1 (out_8[5], and_1_out, and_2_out);
  and and_3 (and_3_out, in_1[4], not_1_out);
  and and_4 (and_4_out, in_4, in_5[4]);
  and and_5 (and_5_out, in_1[3], not_1_out);
  or or_2 (out_8[4], and_3_out, and_4_out);
  and and_6 (and_6_out, in_4, in_5[3]);
  and and_7 (and_7_out, in_1[2], not_1_out);
  or or_3 (out_8[3], and_5_out, and_6_out);
  and and_8 (and_8_out, in_4, in_5[2]);
  and and_9 (and_9_out, in_1[1], not_1_out);
  or or_4 (out_8[2], and_7_out, and_8_out);
  and and_10 (and_10_out, in_4, in_5[1]);
  and and_11 (and_11_out, in_1[0], not_1_out);
  or or_5 (out_8[1], and_9_out, and_10_out);
  and and_12 (and_12_out, in_4, in_5[0]);
  or or_6 (out_8[0], and_11_out, and_12_out);
  and and_13 (and_13_out, in_2[5], not_1_out);
  and and_14 (and_14_out, in_4, in_6[5]);
  and and_15 (and_15_out, in_2[4], not_1_out);
  or or_7 (out_9[5], and_13_out, and_14_out);
  and and_16 (and_16_out, in_4, in_6[4]);
  and and_17 (and_17_out, in_2[3], not_1_out);
  or or_8 (out_9[4], and_15_out, and_16_out);
  and and_18 (and_18_out, in_4, in_6[3]);
  or or_9 (out_9[3], and_17_out, and_18_out);
  and and_19 (and_19_out, in_2[2], not_1_out);
  and and_20 (and_20_out, in_4, in_6[2]);
  and and_21 (and_21_out, in_2[1], not_1_out);
  or or_10 (out_9[2], and_19_out, and_20_out);
  and and_22 (and_22_out, in_4, in_6[1]);
  and and_23 (and_23_out, in_2[0], not_1_out);
  or or_11 (out_9[1], and_21_out, and_22_out);
  and and_24 (and_24_out, in_4, in_6[0]);
  and and_25 (and_25_out, in_3[5], not_1_out);
  or or_12 (out_9[0], and_23_out, and_24_out);
  and and_26 (and_26_out, in_4, in_7[5]);
  and and_27 (and_27_out, in_3[4], not_1_out);
  or or_13 (out_10[5], and_25_out, and_26_out);
  and and_28 (and_28_out, in_4, in_7[4]);
  or or_14 (out_10[4], and_27_out, and_28_out);
  and and_29 (and_29_out, in_3[3], not_1_out);
  and and_30 (and_30_out, in_4, in_7[3]);
  and and_31 (and_31_out, in_3[2], not_1_out);
  or or_15 (out_10[3], and_29_out, and_30_out);
  and and_32 (and_32_out, in_4, in_7[2]);
  and and_33 (and_33_out, in_3[1], not_1_out);
  or or_16 (out_10[2], and_31_out, and_32_out);
  and and_34 (and_34_out, in_4, in_7[1]);
  or or_17 (out_10[1], and_33_out, and_34_out);
  and and_35 (and_35_out, in_3[0], not_1_out);
  and and_36 (and_36_out, in_4, in_7[0]);
  or or_18 (out_10[0], and_35_out, and_36_out);
endmodule
