// Logisim project interpreter.circ as structural Verilog: 1 circuit, main circuit main
module main (
  input  [14:0] in_1,
  input  in_2,
  output [14:0] out_3,
  output [5:0] out_4
);

  wire and_1_out, and_2_out, and_3_out, and_4_out, and_5_out, and_6_out, and_7_out, and_8_out, and_9_out,
       and_10_out, and_11_out, and_12_out, and_13_out, and_14_out, and_15_out, and_16_out, and_17_out,
       and_18_out, and_19_out, and_20_out, and_21_out, and_22_out, and_23_out, and_24_out, and_25_out,
       and_26_out, and_27_out, and_28_out, and_29_out, and_30_out, and_31_out, and_32_out, and_33_out,
       and_34_out, and_35_out, and_36_out, and_37_out, and_38_out, and_39_out, and_40_out, and_41_out,
       and_42_out, and_43_out, and_44_out, and_45_out, and_46_out, and_47_out, and_48_out, and_49_out,
       and_50_out, and_51_out, and_52_out, and_53_out, and_54_out, and_55_out, and_56_out, and_57_out,
       and_58_out, and_59_out, and_60_out, and_61_out, and_62_out, and_63_out, and_64_out, and_65_out,
       and_66_out, and_67_out, and_68_out, and_69_out, and_70_out, and_71_out, and_72_out, and_73_out,
       and_74_out, and_75_out, not_1_out, or_2_out, or_3_out, or_5_out, or_6_out, or_8_out, or_9_out,
       or_11_out, or_12_out, or_14_out, or_15_out, or_17_out, or_18_out, or_20_out, or_21_out, or_23_out,
       or_24_out, or_26_out, or_27_out, or_29_out, or_30_out, or_32_out, or_33_out, or_35_out, or_36_out,
       or_38_out, or_39_out, or_41_out, or_42_out, or_44_out, or_45_out;

  not not_1 (not_1_out, in_2);
  and and_1 (and_1_out, in_1[14], not_1_out);
  and and_2 (and_2_out, in_1[10], in_1[12]);
  and and_3 (and_3_out, 1'b0, in_1[13]);
  and and_4 (and_4_out, 1'b0, in_1[14]);
  and and_5 (and_5_out, in_2, or_3_out);
  or or_1 (out_3[14], and_1_out, and_5_out);
  or or_2 (or_2_out, and_2_out, and_3_out);
  and and_6 (and_6_out, in_1[13], not_1_out);
  and and_7 (and_7_out, in_2, or_6_out);
  and and_8 (and_8_out, in_1[9], in_1[12]);
  and and_9 (and_9_out, 1'b0, in_1[13]);
  and and_10 (and_10_out, 1'b0, in_1[14]);
  or or_3 (or_3_out, or_2_out, and_4_out);
  or or_4 (out_3[13], and_6_out, and_7_out);
  or or_5 (or_5_out, and_8_out, and_9_out);
  and and_11 (and_11_out, in_1[12], not_1_out);
  and and_12 (and_12_out, in_2, or_9_out);
  and and_13 (and_13_out, in_1[8], in_1[12]);
  and and_14 (and_14_out, 1'b0, in_1[13]);
  and and_15 (and_15_out, 1'b0, in_1[14]);
  or or_6 (or_6_out, or_5_out, and_10_out);
  or or_7 (out_3[12], and_11_out, and_12_out);
  or or_8 (or_8_out, and_13_out, and_14_out);
  and and_16 (and_16_out, in_1[11], not_1_out);
  and and_17 (and_17_out, in_1[7], in_1[12]);
  and and_18 (and_18_out, 1'b0, in_1[13]);
  and and_19 (and_19_out, 1'b0, in_1[14]);
  or or_9 (or_9_out, or_8_out, and_15_out);
  or or_10 (out_3[11], and_16_out, and_20_out);
  and and_20 (and_20_out, in_2, or_12_out);
  and and_21 (and_21_out, in_1[10], not_1_out);
  and and_22 (and_22_out, in_1[6], in_1[12]);
  and and_23 (and_23_out, 1'b0, in_1[13]);
  and and_24 (and_24_out, 1'b0, in_1[14]);
  or or_11 (or_11_out, and_17_out, and_18_out);
  or or_12 (or_12_out, or_11_out, and_19_out);
  and and_25 (and_25_out, in_2, or_15_out);
  or or_13 (out_3[10], and_21_out, and_25_out);
  or or_14 (or_14_out, and_22_out, and_23_out);
  and and_26 (and_26_out, in_1[9], not_1_out);
  and and_27 (and_27_out, in_2, or_18_out);
  and and_28 (and_28_out, 1'b0, in_1[12]);
  and and_29 (and_29_out, in_1[10], in_1[13]);
  and and_30 (and_30_out, 1'b0, in_1[14]);
  or or_15 (or_15_out, or_14_out, and_24_out);
  or or_16 (out_3[9], and_26_out, and_27_out);
  or or_17 (or_17_out, and_28_out, and_29_out);
  and and_31 (and_31_out, in_1[8], not_1_out);
  and and_32 (and_32_out, in_2, or_21_out);
  and and_33 (and_33_out, 1'b0, in_1[12]);
  and and_34 (and_34_out, in_1[9], in_1[13]);
  and and_35 (and_35_out, 1'b0, in_1[14]);
  or or_18 (or_18_out, or_17_out, and_30_out);
  or or_19 (out_3[8], and_31_out, and_32_out);
  or or_20 (or_20_out, and_33_out, and_34_out);
  and and_36 (and_36_out, in_1[7], not_1_out);
  and and_37 (and_37_out, 1'b0, in_1[12]);
  and and_38 (and_38_out, in_1[8], in_1[13]);
  and and_39 (and_39_out, 1'b0, in_1[14]);
  or or_21 (or_21_out, or_20_out, and_35_out);
  or or_22 (out_3[7], and_36_out, and_40_out);
  and and_40 (and_40_out, in_2, or_24_out);
  and and_41 (and_41_out, in_1[6], not_1_out);
  and and_42 (and_42_out, 1'b0, in_1[12]);
  and and_43 (and_43_out, in_1[7], in_1[13]);
  and and_44 (and_44_out, 1'b0, in_1[14]);
  or or_23 (or_23_out, and_37_out, and_38_out);
  or or_24 (or_24_out, or_23_out, and_39_out);
  and and_45 (and_45_out, in_2, or_27_out);
  or or_25 (out_3[6], and_41_out, and_45_out);
  or or_26 (or_26_out, and_42_out, and_43_out);
  and and_46 (and_46_out, in_1[5], not_1_out);
  and and_47 (and_47_out, in_2, or_30_out);
  and and_48 (and_48_out, 1'b0, in_1[12]);
  and and_49 (and_49_out, in_1[6], in_1[13]);
  and and_50 (and_50_out, 1'b0, in_1[14]);
  or or_27 (or_27_out, or_26_out, and_44_out);
  or or_28 (out_3[5], and_46_out, and_47_out);
  or or_29 (or_29_out, and_48_out, and_49_out);
  and and_51 (and_51_out, in_1[4], not_1_out);
  and and_52 (and_52_out, in_2, or_33_out);
  and and_53 (and_53_out, 1'b0, in_1[12]);
  and and_54 (and_54_out, 1'b0, in_1[13]);
  and and_55 (and_55_out, in_1[10], in_1[14]);
  or or_30 (or_30_out, or_29_out, and_50_out);
  or or_31 (out_3[4], and_51_out, and_52_out);
  or or_32 (or_32_out, and_53_out, and_54_out);
  and and_56 (and_56_out, in_1[3], not_1_out);
  and and_57 (and_57_out, 1'b0, in_1[12]);
  and and_58 (and_58_out, 1'b0, in_1[13]);
  and and_59 (and_59_out, in_1[9], in_1[14]);
  or or_33 (or_33_out, or_32_out, and_55_out);
  or or_34 (out_3[3], and_56_out, and_60_out);
  and and_60 (and_60_out, in_2, or_36_out);
  and and_61 (and_61_out, in_1[2], not_1_out);
  and and_62 (and_62_out, 1'b0, in_1[12]);
  and and_63 (and_63_out, 1'b0, in_1[13]);
  and and_64 (and_64_out, in_1[8], in_1[14]);
  or or_35 (or_35_out, and_57_out, and_58_out);
  or or_36 (or_36_out, or_35_out, and_59_out);
  and and_65 (and_65_out, in_2, or_39_out);
  or or_37 (out_3[2], and_61_out, and_65_out);
  or or_38 (or_38_out, and_62_out, and_63_out);
  and and_66 (and_66_out, in_1[1], not_1_out);
  and and_67 (and_67_out, in_2, or_42_out);
  and and_68 (and_68_out, 1'b0, in_1[12]);
  and and_69 (and_69_out, 1'b0, in_1[13]);
  and and_70 (and_70_out, in_1[7], in_1[14]);
  or or_39 (or_39_out, or_38_out, and_64_out);
  or or_40 (out_3[1], and_66_out, and_67_out);
  or or_41 (or_41_out, and_68_out, and_69_out);
  and and_71 (and_71_out, in_1[0], not_1_out);
  and and_72 (and_72_out, in_2, or_45_out);
  and and_73 (and_73_out, 1'b0, in_1[12]);
  and and_74 (and_74_out, 1'b0, in_1[13]);
  and and_75 (and_75_out, in_1[6], in_1[14]);
  or or_42 (or_42_out, or_41_out, and_70_out);
  or or_43 (out_3[0], and_71_out, and_72_out);
  or or_44 (or_44_out, and_73_out, and_74_out);
  or or_45 (or_45_out, or_44_out, and_75_out);

  assign out_4 = in_1[5:0];
endmodule
