// Logisim project memory_alt.circ as structural Verilog: 1 circuit, main circuit main
module main (
  input  in_1,
  input  Alt,
  input  in_3,
  input  in_4,
  input  Address,
  input  in_6,
  input  Clock,
  input  W,
  input  R,
  input  P,
  input  in_11,
  input  in_12,
  input  Input,
  input  in_14,
  input  in_15,
  input  in_16,
  output Output,
  output out_18,
  output out_19,
  output out_20,
  output out_21,
  output out_22
);

  wire not_1_out, not_2_out;
  wire [5:0] and_7_out, and_12_out, controlled_buffer_1_out, ram_1_data;

  and and_1 (and_7_out[5], in_1, P);
  RAM #(.addrWidth(3), .dataWidth(6)) ram_1 (
    .addr({in_4, Address, in_6}), .data(ram_1_data), .sel(1'b1), .clk(not_2_out), .ld(not_1_out), .clr(1'b0));
  not not_1 (not_1_out, W);
  not not_2 (not_2_out, Clock);
  and and_2 (and_7_out[4], Alt, P);
  assign controlled_buffer_1_out = R ? ram_1_data : 6'bz;  // Controlled_Buffer controlled_buffer_1
  assign ram_1_data = W ? {in_11, in_12, Input, in_14, in_15, in_16} : 6'bz;  // Controlled_Buffer controlled_buffer_2
  or or_1 (Output, and_7_out[5], and_12_out[5]);
  and and_3 (and_7_out[3], in_3, P);
  or or_2 (out_18, and_7_out[4], and_12_out[4]);
  and and_4 (and_7_out[2], in_4, P);
  or or_3 (out_19, and_7_out[3], and_12_out[3]);
  and and_5 (and_7_out[1], Address, P);
  and and_6 (and_12_out[5], controlled_buffer_1_out[5], R);
  or or_4 (out_20, and_7_out[2], and_12_out[2]);
  and and_7 (and_7_out[0], in_6, P);
  and and_8 (and_12_out[4], controlled_buffer_1_out[4], R);
  or or_5 (out_21, and_7_out[1], and_12_out[1]);
  and and_9 (and_12_out[3], controlled_buffer_1_out[3], R);
  or or_6 (out_22, and_7_out[0], and_12_out[0]);
  and and_10 (and_12_out[2], controlled_buffer_1_out[2], R);
  and and_11 (and_12_out[1], controlled_buffer_1_out[1], R);
  and and_12 (and_12_out[0], controlled_buffer_1_out[0], R);
endmodule
