// Logisim project memory_small.circ as structural Verilog: 1 circuit, main circuit main
module main (
  input  Pass,
  input  in_2,
  input  in_3,
  input  in_4,
  input  Address,
  input  in_6,
  input  Write,
  input  in_8,
  input  Read,
  input  Initialise,
  input  in_11,
  input  in_12,
  input  Input,
  input  in_14,
  input  in_15,
  input  in_16,
  output out_17,
  output out_18,
  output Output,
  output out_20,
  output out_21,
  output out_22
);

  wire and_1_out, and_2_out, and_3_out, and_4_out, and_5_out, and_6_out, and_7_out, and_8_out, and_9_out,
       and_10_out, and_11_out, and_12_out, and_13_out, and_14_out, and_15_out, and_16_out, and_17_out,
       and_18_out, and_19_out, and_20_out, and_21_out, and_22_out, and_23_out, and_24_out, and_25_out,
       and_26_out, and_27_out, and_28_out, nand_1_out, nand_2_out, nand_3_out, nand_4_out, nand_5_out,
       nand_6_out, nand_7_out, nand_8_out, nand_9_out, nand_10_out, nand_11_out, nand_12_out, nand_13_out,
       nand_14_out, nand_15_out, nand_16_out, nand_17_out, nand_18_out, nand_19_out, nand_20_out,
       nand_21_out, nand_22_out, nand_23_out, nand_24_out, nand_25_out, nand_26_out, nand_27_out,
       nand_28_out, nand_29_out, nand_30_out, nand_31_out, nand_32_out, nand_33_out, nand_34_out,
       nand_35_out, nand_36_out, nand_37_out, nand_38_out, nand_39_out, nand_40_out, nand_41_out,
       nand_42_out, nand_43_out, nand_44_out, nand_45_out, nand_46_out, nand_47_out, nand_48_out, not_1_out,
       not_2_out, not_3_out, not_4_out, not_5_out, not_6_out, not_7_out, not_8_out, not_9_out, not_10_out,
       not_11_out, not_12_out, or_1_out, or_2_out, or_6_out, or_7_out, or_9_out, or_10_out, or_12_out,
       or_13_out, xnor_1_out, xnor_2_out, xnor_3_out, xnor_4_out, xnor_5_out, xnor_6_out, xnor_7_out,
       xnor_8_out, xnor_9_out, xnor_10_out;

  xnor xnor_1 (xnor_1_out, Read, 1'b1);
  xnor xnor_2 (xnor_2_out, in_8, 1'b0);
  xnor xnor_3 (xnor_3_out, Read, 1'b0);
  xnor xnor_4 (xnor_4_out, in_8, 1'b1);
  xnor xnor_5 (xnor_5_out, Write, 1'b1);
  xnor xnor_6 (xnor_6_out, in_6, 1'b0);
  xnor xnor_7 (xnor_7_out, Address, 1'b0);
  xnor xnor_8 (xnor_8_out, Write, 1'b0);
  xnor xnor_9 (xnor_9_out, in_6, 1'b1);
  xnor xnor_10 (xnor_10_out, Address, 1'b0);
  and and_1 (and_1_out, xnor_1_out, xnor_2_out);
  and and_2 (and_2_out, xnor_3_out, xnor_4_out);
  and and_3 (and_3_out, xnor_5_out, xnor_6_out);
  and and_4 (and_4_out, xnor_8_out, xnor_9_out);
  and and_5 (and_5_out, and_3_out, xnor_7_out);
  and and_6 (and_6_out, and_4_out, xnor_10_out);
  and and_7 (and_7_out, and_1_out, and_5_out);
  and and_8 (and_8_out, and_2_out, and_5_out);
  and and_9 (and_9_out, and_1_out, and_6_out);
  and and_10 (and_10_out, and_2_out, and_6_out);
  or or_1 (or_1_out, Initialise, and_8_out);
  or or_2 (or_2_out, Initialise, and_10_out);
  or or_3 (out_17, or_6_out, and_11_out);
  and and_11 (and_11_out, Pass, in_2);
  or or_4 (out_18, or_7_out, and_12_out);
  and and_12 (and_12_out, Pass, in_3);
  or or_5 (Output, or_9_out, and_13_out);
  and and_13 (and_13_out, Pass, in_4);
  or or_6 (or_6_out, and_18_out, and_17_out);
  and and_14 (and_14_out, Pass, Address);
  or or_7 (or_7_out, and_20_out, and_19_out);
  or or_8 (out_20, or_10_out, and_14_out);
  or or_9 (or_9_out, and_22_out, and_21_out);
  or or_10 (or_10_out, and_24_out, and_23_out);
  or or_11 (out_21, or_12_out, and_15_out);
  and and_15 (and_15_out, Pass, in_6);
  or or_12 (or_12_out, and_26_out, and_25_out);
  or or_13 (or_13_out, and_28_out, and_27_out);
  or or_14 (out_22, or_13_out, and_16_out);
  and and_16 (and_16_out, Pass, Write);
  not not_1 (not_1_out, in_11);
  nand nand_1 (nand_1_out, not_1_out, or_1_out);
  nand nand_2 (nand_2_out, or_1_out, in_11);
  not not_2 (not_2_out, in_11);
  nand nand_3 (nand_3_out, not_2_out, or_2_out);
  nand nand_4 (nand_4_out, or_2_out, in_11);
  nand nand_5 (nand_5_out, nand_1_out, nand_6_out);
  nand nand_6 (nand_6_out, nand_5_out, nand_2_out);
  nand nand_7 (nand_7_out, nand_3_out, nand_8_out);
  nand nand_8 (nand_8_out, nand_7_out, nand_4_out);
  and and_17 (and_17_out, and_7_out, nand_6_out);
  and and_18 (and_18_out, and_9_out, nand_8_out);
  not not_3 (not_3_out, in_12);
  not not_4 (not_4_out, in_12);
  nand nand_9 (nand_9_out, not_3_out, or_1_out);
  nand nand_10 (nand_10_out, or_1_out, in_12);
  nand nand_11 (nand_11_out, not_4_out, or_2_out);
  nand nand_12 (nand_12_out, or_2_out, in_12);
  nand nand_13 (nand_13_out, nand_9_out, nand_14_out);
  nand nand_14 (nand_14_out, nand_13_out, nand_10_out);
  nand nand_15 (nand_15_out, nand_11_out, nand_16_out);
  nand nand_16 (nand_16_out, nand_15_out, nand_12_out);
  and and_19 (and_19_out, and_7_out, nand_14_out);
  and and_20 (and_20_out, and_9_out, nand_16_out);
  not not_5 (not_5_out, Input);
  not not_6 (not_6_out, Input);
  nand nand_17 (nand_17_out, not_5_out, or_1_out);
  nand nand_18 (nand_18_out, or_1_out, Input);
  nand nand_19 (nand_19_out, not_6_out, or_2_out);
  nand nand_20 (nand_20_out, or_2_out, Input);
  nand nand_21 (nand_21_out, nand_17_out, nand_22_out);
  nand nand_22 (nand_22_out, nand_21_out, nand_18_out);
  nand nand_23 (nand_23_out, nand_19_out, nand_24_out);
  nand nand_24 (nand_24_out, nand_23_out, nand_20_out);
  and and_21 (and_21_out, and_7_out, nand_22_out);
  and and_22 (and_22_out, and_9_out, nand_24_out);
  not not_7 (not_7_out, in_14);
  not not_8 (not_8_out, in_14);
  nand nand_25 (nand_25_out, not_7_out, or_1_out);
  nand nand_26 (nand_26_out, or_1_out, in_14);
  nand nand_27 (nand_27_out, not_8_out, or_2_out);
  nand nand_28 (nand_28_out, or_2_out, in_14);
  nand nand_29 (nand_29_out, nand_25_out, nand_30_out);
  nand nand_30 (nand_30_out, nand_29_out, nand_26_out);
  nand nand_31 (nand_31_out, nand_27_out, nand_32_out);
  nand nand_32 (nand_32_out, nand_31_out, nand_28_out);
  and and_23 (and_23_out, and_7_out, nand_30_out);
  and and_24 (and_24_out, and_9_out, nand_32_out);
  not not_9 (not_9_out, in_15);
  nand nand_33 (nand_33_out, not_9_out, or_1_out);
  nand nand_34 (nand_34_out, or_1_out, in_15);
  not not_10 (not_10_out, in_15);
  nand nand_35 (nand_35_out, not_10_out, or_2_out);
  nand nand_36 (nand_36_out, or_2_out, in_15);
  nand nand_37 (nand_37_out, nand_33_out, nand_38_out);
  nand nand_38 (nand_38_out, nand_37_out, nand_34_out);
  nand nand_39 (nand_39_out, nand_35_out, nand_40_out);
  nand nand_40 (nand_40_out, nand_39_out, nand_36_out);
  and and_25 (and_25_out, and_7_out, nand_38_out);
  and and_26 (and_26_out, and_9_out, nand_40_out);
  not not_11 (not_11_out, in_16);
  not not_12 (not_12_out, in_16);
  nand nand_41 (nand_41_out, not_11_out, or_1_out);
  nand nand_42 (nand_42_out, or_1_out, in_16);
  nand nand_43 (nand_43_out, not_12_out, or_2_out);
  nand nand_44 (nand_44_out, or_2_out, in_16);
  nand nand_45 (nand_45_out, nand_41_out, nand_46_out);
  nand nand_46 (nand_46_out, nand_45_out, nand_42_out);
  nand nand_47 (nand_47_out, nand_43_out, nand_48_out);
  nand nand_48 (nand_48_out, nand_47_out, nand_44_out);
  and and_27 (and_27_out, and_7_out, nand_46_out);
  and and_28 (and_28_out, and_9_out, nand_48_out);
endmodule
