// Logisim project numpad.circ as structural Verilog: 1 circuit, main circuit main
module main (
  input  in_1,
  input  in_2,
  input  in_3,
  input  in_4,
  input  in_5,
  input  in_6,
  input  in_7,
  input  in_8,
  input  in_9,
  input  in_10,
  input  in_11,
  input  in_12,
  output out_13,
  output out_14,
  output out_15,
  output out_16,
  output out_17,
  output out_18
);

  wire and_1_out, and_2_out, and_3_out, and_4_out, and_5_out, and_6_out, and_7_out, and_8_out, and_9_out,
       and_10_out, and_11_out, and_12_out, and_13_out, and_14_out, and_15_out, and_16_out, and_17_out,
       and_18_out, and_19_out, and_20_out, and_21_out, and_22_out, and_23_out, and_24_out, and_25_out,
       and_26_out, and_27_out, and_28_out, and_29_out, and_30_out, and_31_out, and_32_out, and_33_out,
       and_34_out, and_35_out, and_36_out, and_37_out, and_38_out, and_39_out, and_40_out, and_41_out,
       and_42_out, and_43_out, and_44_out, and_45_out, and_46_out, main_2_out_17, main_2_out_18,
       main_2_out_19, nand_1_out, nand_2_out, nand_3_out, nand_4_out, nand_5_out, nand_6_out, nand_7_out,
       nand_8_out, nand_9_out, nand_10_out, nand_11_out, nand_12_out, nand_13_out, nand_14_out, nand_15_out,
       nand_16_out, nand_17_out, nand_18_out, nand_19_out, nand_20_out, nand_21_out, nand_22_out,
       nand_23_out, nand_24_out, nand_25_out, nand_26_out, nand_27_out, nand_28_out, nand_29_out,
       nand_30_out, nand_31_out, nand_32_out, not_1_out, not_2_out, not_3_out, not_4_out, not_5_out,
       not_6_out, not_7_out, not_8_out, not_9_out, not_10_out, or_1_out, or_2_out, or_3_out, or_4_out,
       or_5_out, or_6_out, or_7_out, or_8_out, or_9_out, or_10_out, or_11_out, or_12_out, or_13_out,
       or_14_out, or_15_out, or_16_out, or_17_out, or_18_out, or_19_out, or_20_out, or_21_out, or_22_out,
       or_23_out, or_24_out, or_25_out, or_26_out, or_27_out, or_28_out, or_29_out, or_30_out, or_31_out,
       or_32_out, or_33_out, or_34_out, or_35_out, or_36_out, or_37_out, or_38_out, or_39_out, or_40_out,
       or_41_out, or_42_out, or_43_out, or_44_out, or_45_out, or_46_out;

  or or_1 (or_1_out, in_4, or_2_out);
  or or_2 (or_2_out, in_5, or_3_out);
  or or_3 (or_3_out, in_6, or_4_out);
  or or_4 (or_4_out, in_7, or_5_out);
  or or_5 (or_5_out, in_8, or_6_out);
  or or_6 (or_6_out, in_9, or_7_out);
  or or_7 (or_7_out, in_10, or_8_out);
  or or_8 (or_8_out, in_11, in_12);
  and and_1 (and_1_out, in_1, or_1_out);
  and and_2 (and_2_out, in_2, or_1_out);
  not not_1 (not_1_out, in_3);
  and and_3 (and_3_out, in_4, 1'b1);
  and and_4 (and_4_out, in_5, 1'b1);
  and and_5 (and_5_out, in_6, 1'b0);
  and and_6 (and_6_out, in_7, 1'b0);
  and and_7 (and_7_out, in_8, 1'b0);
  and and_8 (and_8_out, in_9, 1'b0);
  and and_9 (and_9_out, in_10, 1'b0);
  and and_10 (and_10_out, in_11, 1'b0);
  and and_11 (and_11_out, in_12, 1'b0);
  or or_9 (or_9_out, and_2_out, in_3);
  and and_12 (and_12_out, not_1_out, or_37_out);
  and and_13 (and_13_out, not_1_out, or_28_out);
  and and_14 (and_14_out, not_1_out, or_19_out);
  and and_15 (and_15_out, not_1_out, or_10_out);
  or or_10 (or_10_out, and_3_out, or_11_out);
  or or_11 (or_11_out, and_4_out, or_12_out);
  or or_12 (or_12_out, and_5_out, or_13_out);
  or or_13 (or_13_out, and_6_out, or_14_out);
  or or_14 (or_14_out, and_7_out, or_15_out);
  or or_15 (or_15_out, and_8_out, or_16_out);
  or or_16 (or_16_out, and_9_out, or_17_out);
  or or_17 (or_17_out, and_10_out, or_18_out);
  or or_18 (or_18_out, and_11_out, 1'b0);
  not not_2 (not_2_out, and_12_out);
  not not_3 (not_3_out, and_13_out);
  not not_4 (not_4_out, and_14_out);
  not not_5 (not_5_out, and_15_out);
  and and_16 (and_16_out, in_4, 1'b0);
  and and_17 (and_17_out, in_5, 1'b0);
  and and_18 (and_18_out, in_6, 1'b1);
  and and_19 (and_19_out, in_7, 1'b1);
  and and_20 (and_20_out, in_8, 1'b1);
  and and_21 (and_21_out, in_9, 1'b1);
  and and_22 (and_22_out, in_10, 1'b0);
  and and_23 (and_23_out, in_11, 1'b0);
  and and_24 (and_24_out, in_12, 1'b0);
  nand nand_1 (nand_1_out, not_2_out, or_9_out);
  nand nand_2 (nand_2_out, or_9_out, and_12_out);
  nand nand_3 (nand_3_out, not_3_out, or_9_out);
  nand nand_4 (nand_4_out, or_9_out, and_13_out);
  nand nand_5 (nand_5_out, not_4_out, or_9_out);
  nand nand_6 (nand_6_out, or_9_out, and_14_out);
  nand nand_7 (nand_7_out, not_5_out, or_9_out);
  nand nand_8 (nand_8_out, or_9_out, and_15_out);
  or or_19 (or_19_out, and_16_out, or_20_out);
  or or_20 (or_20_out, and_17_out, or_21_out);
  or or_21 (or_21_out, and_18_out, or_22_out);
  or or_22 (or_22_out, and_19_out, or_23_out);
  or or_23 (or_23_out, and_20_out, or_24_out);
  or or_24 (or_24_out, and_21_out, or_25_out);
  or or_25 (or_25_out, and_22_out, or_26_out);
  or or_26 (or_26_out, and_23_out, or_27_out);
  or or_27 (or_27_out, and_24_out, 1'b0);
  addition_main main_1 (
    .in_1(main_2_out_17), .in_2(main_2_out_18), .in_3(main_2_out_19), .in_4(nand_28_out), .in_5(nand_26_out),
    .in_6(1'b0), .in_7(1'b0), .in_8(1'b0), .in_9(nand_16_out), .in_10(nand_14_out), .in_11(nand_12_out),
    .in_12(nand_10_out), .out_14(out_13), .out_15(out_14), .out_16(out_15), .out_17(out_16), .out_18(out_17),
    .out_19(out_18));  // open: out_13
  and and_25 (and_25_out, in_4, 1'b0);
  and and_26 (and_26_out, in_5, 1'b0);
  and and_27 (and_27_out, in_6, 1'b1);
  and and_28 (and_28_out, in_7, 1'b1);
  and and_29 (and_29_out, in_8, 1'b0);
  and and_30 (and_30_out, in_9, 1'b0);
  and and_31 (and_31_out, in_10, 1'b1);
  and and_32 (and_32_out, in_11, 1'b1);
  and and_33 (and_33_out, in_12, 1'b0);
  nand nand_9 (nand_9_out, nand_1_out, nand_10_out);
  nand nand_10 (nand_10_out, nand_9_out, nand_2_out);
  nand nand_11 (nand_11_out, nand_3_out, nand_12_out);
  nand nand_12 (nand_12_out, nand_11_out, nand_4_out);
  nand nand_13 (nand_13_out, nand_5_out, nand_14_out);
  nand nand_14 (nand_14_out, nand_13_out, nand_6_out);
  nand nand_15 (nand_15_out, nand_7_out, nand_16_out);
  nand nand_16 (nand_16_out, nand_15_out, nand_8_out);
  or or_28 (or_28_out, and_25_out, or_29_out);
  or or_29 (or_29_out, and_26_out, or_30_out);
  or or_30 (or_30_out, and_27_out, or_31_out);
  or or_31 (or_31_out, and_28_out, or_32_out);
  or or_32 (or_32_out, and_29_out, or_33_out);
  or or_33 (or_33_out, and_30_out, or_34_out);
  or or_34 (or_34_out, and_31_out, or_35_out);
  or or_35 (or_35_out, and_32_out, or_36_out);
  or or_36 (or_36_out, and_33_out, 1'b0);
  and and_34 (and_34_out, in_4, 1'b1);
  and and_35 (and_35_out, in_5, 1'b0);
  and and_36 (and_36_out, in_6, 1'b1);
  and and_37 (and_37_out, in_7, 1'b0);
  and and_38 (and_38_out, in_8, 1'b1);
  and and_39 (and_39_out, in_9, 1'b0);
  and and_40 (and_40_out, in_10, 1'b1);
  and and_41 (and_41_out, in_11, 1'b0);
  and and_42 (and_42_out, in_12, 1'b1);
  not not_6 (not_6_out, in_3);
  or or_37 (or_37_out, and_34_out, or_38_out);
  or or_38 (or_38_out, and_35_out, or_39_out);
  or or_39 (or_39_out, and_36_out, or_40_out);
  or or_40 (or_40_out, and_37_out, or_41_out);
  or or_41 (or_41_out, and_38_out, or_42_out);
  or or_42 (or_42_out, and_39_out, or_43_out);
  or or_43 (or_43_out, and_40_out, or_44_out);
  or or_44 (or_44_out, and_41_out, or_45_out);
  or or_45 (or_45_out, and_42_out, 1'b0);
  or or_46 (or_46_out, and_1_out, in_3);
  and and_43 (and_43_out, not_6_out, or_37_out);
  and and_44 (and_44_out, not_6_out, or_28_out);
  and and_45 (and_45_out, not_6_out, or_19_out);
  and and_46 (and_46_out, not_6_out, or_10_out);
  addition_main main_2 (
    .in_1(1'b0), .in_2(1'b0), .in_3(1'b0), .in_4(1'b0), .in_5(nand_32_out), .in_6(nand_30_out), .in_7(1'b0),
    .in_8(1'b0), .in_9(nand_32_out), .in_10(nand_30_out), .in_11(nand_28_out), .in_12(nand_26_out),
    .out_17(main_2_out_17), .out_18(main_2_out_18), .out_19(main_2_out_19));  // open: out_13, out_14, out_15, out_16
  not not_7 (not_7_out, and_43_out);
  not not_8 (not_8_out, and_44_out);
  not not_9 (not_9_out, and_45_out);
  not not_10 (not_10_out, and_46_out);
  nand nand_17 (nand_17_out, not_7_out, or_46_out);
  nand nand_18 (nand_18_out, or_46_out, and_43_out);
  nand nand_19 (nand_19_out, not_8_out, or_46_out);
  nand nand_20 (nand_20_out, or_46_out, and_44_out);
  nand nand_21 (nand_21_out, not_9_out, or_46_out);
  nand nand_22 (nand_22_out, or_46_out, and_45_out);
  nand nand_23 (nand_23_out, not_10_out, or_46_out);
  nand nand_24 (nand_24_out, or_46_out, and_46_out);
  nand nand_25 (nand_25_out, nand_17_out, nand_26_out);
  nand nand_26 (nand_26_out, nand_25_out, nand_18_out);
  nand nand_27 (nand_27_out, nand_19_out, nand_28_out);
  nand nand_28 (nand_28_out, nand_27_out, nand_20_out);
  nand nand_29 (nand_29_out, nand_21_out, nand_30_out);
  nand nand_30 (nand_30_out, nand_29_out, nand_22_out);
  nand nand_31 (nand_31_out, nand_23_out, nand_32_out);
  nand nand_32 (nand_32_out, nand_31_out, nand_24_out);
endmodule
