// Logisim project output selector.circ as structural Verilog: 1 circuit, main circuit main
module main (
  input  in_1,
  input  in_2,
  input  in_3,
  input  in_4,
  input  in_5,
  input  in_6,
  input  in_7,
  input  in_8,
  input  in_9,
  input  in_10,
  input  in_11,
  input  in_12,
  input  in_13,
  output out_14,
  output out_15,
  output out_16,
  output out_17,
  output out_18,
  output out_19
);

  wire and_1_out, and_2_out, and_3_out, and_4_out, and_5_out, and_6_out;

  and and_1 (and_1_out, in_7, in_8);
  or or_1 (out_14, in_1, and_1_out);
  and and_2 (and_2_out, in_7, in_9);
  or or_2 (out_15, in_2, and_2_out);
  and and_3 (and_3_out, in_7, in_10);
  or or_3 (out_16, in_3, and_3_out);
  and and_4 (and_4_out, in_7, in_11);
  or or_4 (out_17, in_4, and_4_out);
  and and_5 (and_5_out, in_7, in_12);
  or or_5 (out_18, in_5, and_5_out);
  and and_6 (and_6_out, in_7, in_13);
  or or_6 (out_19, in_6, and_6_out);
endmodule
