// Logisim project program counter - alt.circ as structural Verilog: 1 circuit, main circuit main
module main (
  input  in_1,
  input  in_2,
  input  in_3,
  input  in_4,
  input  in_5,
  input  in_6,
  input  in_7,
  input  in_8,
  output out_9,
  output out_10,
  output out_11,
  output out_12,
  output out_13,
  output out_14
);

  wire not_1_out, or_1_out, or_2_out, or_3_out, or_4_out, or_5_out;

  or or_1 (or_1_out, in_2, in_1);
  or or_2 (or_2_out, or_1_out, or_3_out);
  or or_3 (or_3_out, in_4, in_3);
  not not_1 (not_1_out, or_4_out);
  or or_4 (or_4_out, or_2_out, or_5_out);
  or or_5 (or_5_out, in_6, in_5);
  Counter #(.width(6), .max('h3f)) counter_1 (
    .load(or_4_out), .D({in_1, in_2, in_3, in_4, in_5, in_6}), .count(not_1_out),
    .Q({out_9, out_10, out_11, out_12, out_13, out_14}), .clk(in_8), .clr(in_7));  // open: carry

  // Notes on the sheet:
  //   Initialise/Reset Counter
  //   Pulse for counter
endmodule
