// Logisim project program counter.circ as structural Verilog: 1 circuit, main circuit main
module main (
  input  in_1,
  input  in_2,
  input  in_3,
  input  in_4,
  input  in_5,
  input  in_6,
  input  in_7,
  input  in_8,
  output out_9,
  output out_10,
  output out_11,
  output out_12,
  output out_13,
  output out_14
);

  wire and_1_out, and_2_out, and_3_out, and_4_out, and_5_out, and_6_out, and_7_out, and_8_out, and_9_out,
       and_10_out, and_11_out, and_12_out, and_13_out, and_14_out, and_15_out, and_16_out, and_17_out,
       and_18_out, and_19_out, and_20_out, and_21_out, and_22_out, and_23_out, nand_1_out, nand_2_out,
       nand_3_out, nand_4_out, nand_5_out, nand_6_out, nand_7_out, nand_8_out, nand_9_out, nand_10_out,
       nand_11_out, nand_12_out, nand_13_out, nand_14_out, nand_15_out, nand_16_out, nand_17_out,
       nand_18_out, nand_19_out, nand_20_out, nand_21_out, nand_22_out, nand_23_out, nand_24_out,
       nand_25_out, nand_26_out, nand_27_out, nand_28_out, nand_29_out, nand_30_out, nand_31_out,
       nand_32_out, nand_33_out, nand_34_out, nand_35_out, nand_36_out, nand_37_out, nand_39_out,
       nand_41_out, nand_43_out, nand_45_out, nand_47_out, not_1_out, not_2_out, not_3_out, not_4_out,
       not_5_out, not_6_out, not_7_out, not_8_out, not_9_out, not_10_out, not_11_out, not_12_out, not_13_out,
       not_14_out, or_1_out, or_2_out, or_3_out, or_4_out, or_5_out, or_6_out, or_7_out, or_8_out, or_9_out,
       or_10_out, or_11_out, or_12_out, or_13_out, xor_1_out, xor_2_out, xor_3_out, xor_4_out, xor_5_out,
       xor_6_out;

  not not_1 (not_1_out, in_8);
  LED led_1 (.in(out_9));
  and and_1 (and_1_out, out_9, in_8);
  LED led_2 (.in(out_10));
  LED led_3 (.in(and_1_out));
  LED led_4 (.in(out_11));
  and and_2 (and_2_out, out_10, in_8);
  LED led_5 (.in(and_2_out));
  LED led_6 (.in(out_12));
  and and_3 (and_3_out, out_11, in_8);
  LED led_7 (.in(and_3_out));
  LED led_8 (.in(out_13));
  and and_4 (and_4_out, out_12, in_8);
  LED led_9 (.in(and_4_out));
  and and_5 (and_5_out, out_13, in_8);
  LED led_10 (.in(out_14));
  and and_6 (and_6_out, out_14, in_8);
  LED led_11 (.in(and_5_out));
  xor xor_1 (xor_1_out, and_2_out, and_9_out);
  and and_7 (and_7_out, and_2_out, and_9_out);
  xor xor_2 (xor_2_out, and_1_out, and_7_out);
  or or_1 (or_1_out, in_1, 1'b0);
  or or_2 (or_2_out, in_2, or_1_out);
  LED led_12 (.in(and_6_out));
  xor xor_3 (xor_3_out, and_4_out, and_11_out);
  and and_8 (and_8_out, and_4_out, and_11_out);
  xor xor_4 (xor_4_out, and_3_out, and_8_out);
  and and_9 (and_9_out, and_3_out, and_8_out);
  or or_3 (or_3_out, in_3, or_2_out);
  xor xor_5 (xor_5_out, and_6_out, in_8);
  and and_10 (and_10_out, and_6_out, in_8);
  xor xor_6 (xor_6_out, and_5_out, and_10_out);
  and and_11 (and_11_out, and_5_out, and_10_out);
  or or_4 (or_4_out, in_4, or_3_out);
  or or_5 (or_5_out, in_5, or_4_out);
  not not_2 (not_2_out, or_6_out);
  or or_6 (or_6_out, in_6, or_5_out);
  and and_12 (and_12_out, xor_5_out, not_2_out);
  and and_13 (and_13_out, xor_6_out, not_2_out);
  and and_14 (and_14_out, xor_3_out, not_2_out);
  and and_15 (and_15_out, xor_4_out, not_2_out);
  and and_16 (and_16_out, xor_1_out, not_2_out);
  and and_17 (and_17_out, xor_2_out, not_2_out);
  and and_18 (and_18_out, in_6, or_6_out);
  and and_19 (and_19_out, in_5, or_6_out);
  and and_20 (and_20_out, in_4, or_6_out);
  and and_21 (and_21_out, in_3, or_6_out);
  and and_22 (and_22_out, in_2, or_6_out);
  and and_23 (and_23_out, in_1, or_6_out);
  or or_7 (or_7_out, in_7, in_8);
  not not_3 (not_3_out, or_8_out);
  or or_8 (or_8_out, and_18_out, and_12_out);
  not not_4 (not_4_out, or_9_out);
  or or_9 (or_9_out, and_19_out, and_13_out);
  not not_5 (not_5_out, or_10_out);
  or or_10 (or_10_out, and_20_out, and_14_out);
  or or_11 (or_11_out, and_21_out, and_15_out);
  not not_6 (not_6_out, or_11_out);
  not not_7 (not_7_out, or_12_out);
  or or_12 (or_12_out, and_22_out, and_16_out);
  not not_8 (not_8_out, or_13_out);
  or or_13 (or_13_out, and_23_out, and_17_out);
  nand nand_1 (nand_1_out, not_3_out, or_7_out);
  nand nand_2 (nand_2_out, or_7_out, or_8_out);
  nand nand_3 (nand_3_out, not_4_out, or_7_out);
  nand nand_4 (nand_4_out, or_7_out, or_9_out);
  nand nand_5 (nand_5_out, not_5_out, or_7_out);
  nand nand_6 (nand_6_out, or_7_out, or_10_out);
  nand nand_7 (nand_7_out, not_6_out, or_7_out);
  nand nand_8 (nand_8_out, or_7_out, or_11_out);
  nand nand_9 (nand_9_out, not_7_out, or_7_out);
  nand nand_10 (nand_10_out, or_7_out, or_12_out);
  nand nand_11 (nand_11_out, not_8_out, or_7_out);
  nand nand_12 (nand_12_out, or_7_out, or_13_out);
  nand nand_13 (nand_13_out, nand_1_out, nand_14_out);
  nand nand_14 (nand_14_out, nand_13_out, nand_2_out);
  nand nand_15 (nand_15_out, nand_3_out, nand_16_out);
  nand nand_16 (nand_16_out, nand_15_out, nand_4_out);
  nand nand_17 (nand_17_out, nand_5_out, nand_18_out);
  nand nand_18 (nand_18_out, nand_17_out, nand_6_out);
  nand nand_19 (nand_19_out, nand_7_out, nand_20_out);
  nand nand_20 (nand_20_out, nand_19_out, nand_8_out);
  nand nand_21 (nand_21_out, nand_9_out, nand_22_out);
  nand nand_22 (nand_22_out, nand_21_out, nand_10_out);
  nand nand_23 (nand_23_out, nand_11_out, nand_24_out);
  nand nand_24 (nand_24_out, nand_23_out, nand_12_out);
  LED led_13 (.in(nand_14_out));
  LED led_14 (.in(nand_16_out));
  LED led_15 (.in(nand_18_out));
  LED led_16 (.in(nand_20_out));
  LED led_17 (.in(nand_22_out));
  LED led_18 (.in(nand_24_out));
  not not_9 (not_9_out, nand_14_out);
  not not_10 (not_10_out, nand_16_out);
  not not_11 (not_11_out, nand_18_out);
  not not_12 (not_12_out, nand_20_out);
  not not_13 (not_13_out, nand_22_out);
  not not_14 (not_14_out, nand_24_out);
  nand nand_25 (nand_25_out, not_9_out, not_1_out);
  nand nand_26 (nand_26_out, not_1_out, nand_14_out);
  nand nand_27 (nand_27_out, not_10_out, not_1_out);
  nand nand_28 (nand_28_out, not_1_out, nand_16_out);
  nand nand_29 (nand_29_out, not_11_out, not_1_out);
  nand nand_30 (nand_30_out, not_1_out, nand_18_out);
  nand nand_31 (nand_31_out, not_12_out, not_1_out);
  nand nand_32 (nand_32_out, not_1_out, nand_20_out);
  nand nand_33 (nand_33_out, not_13_out, not_1_out);
  nand nand_34 (nand_34_out, not_1_out, nand_22_out);
  nand nand_35 (nand_35_out, not_14_out, not_1_out);
  nand nand_36 (nand_36_out, not_1_out, nand_24_out);
  nand nand_37 (nand_37_out, nand_25_out, out_14);
  nand nand_38 (out_14, nand_37_out, nand_26_out);
  nand nand_39 (nand_39_out, nand_27_out, out_13);
  nand nand_40 (out_13, nand_39_out, nand_28_out);
  nand nand_41 (nand_41_out, nand_29_out, out_12);
  nand nand_42 (out_12, nand_41_out, nand_30_out);
  nand nand_43 (nand_43_out, nand_31_out, out_11);
  nand nand_44 (out_11, nand_43_out, nand_32_out);
  nand nand_45 (nand_45_out, nand_33_out, out_10);
  nand nand_46 (out_10, nand_45_out, nand_34_out);
  nand nand_47 (nand_47_out, nand_35_out, out_9);
  nand nand_48 (out_9, nand_47_out, nand_36_out);

  // Notes on the sheet:
  //   Initialise/Reset Counter
  //   Pulse for counter
  //   Counted value
endmodule
