// Logisim project rudimentary computing device.circ as structural Verilog: 1 circuit, main circuit main
module main (
  input  in_1,
  input  [5:0] A,
  input  [5:0] B,
  input  [5:0] C,
  output [5:0] out_5,
  output [5:0] A_2,
  output [5:0] B_2,
  output [5:0] C_2
);

  wire and_1_out, and_2_out, and_3_out, and_4_out, and_5_out, and_6_out, and_7_out, and_8_out, and_10_out,
       button_1_out, button_2_out, clock_1_out, main_6_a_b, main_6_a_b_2, main_6_a_b_3, main_6_add,
       main_6_halt, main_6_insert, main_6_invert, main_6_out, main_6_out_14, main_6_out_15, main_6_out_16,
       main_6_out_17, main_6_step, not_1_out, or_1_out;
  wire [0:0] main_12_equality_check, main_13_out_13, main_14_out_13;
  wire [5:0] and_15_out, main_8_out_3, main_9_out_3, main_10_out_3, main_11_out_4, main_15_out_12,
       main_17_out_19, main_19_to_a, main_19_to_b, main_19_to_c, main_20_out_23, main_21_out_23,
       main_22_out_23, main_23_out_8, main_23_out_9, main_23_out_10, main_24_out_8, main_24_out_9,
       main_24_out_10, main_25_out_8, main_25_out_9, main_25_out_10, main_26_out_8, main_26_out_9,
       main_26_out_10, main_27_out_8, main_27_out_9, main_27_out_10, main_28_out_8, main_28_out_9,
       main_28_out_10, main_29_out_8, main_29_out_9, main_29_out_10, main_30_out_8, main_30_out_9,
       main_30_out_10, main_31_out_8, main_31_out_9, main_31_out_10, main_32_out_8, main_32_out_9,
       main_32_out_10, main_33_out_8, main_33_out_9, main_33_out_10;
  wire [7:0] main_1_out_2, main_1_out_2_2, main_2_out_2, main_2_out_2_2, main_4_out_2, main_4_out_2_2,
       main_5_out_2, main_5_out_2_2, main_7_out_2, main_7_out_2_2, main_18_out_2, main_18_out_2_2;
  wire [31:0] rom_1_data;

  _7_Segment_Display u_7_segment_display_1 (
    .g(main_1_out_2[7]), .f(main_1_out_2[6]), .a(main_1_out_2[5]), .b(main_1_out_2[4]),
    .e(main_1_out_2_2[7]), .d(main_1_out_2_2[6]), .c(main_1_out_2_2[5]), .dp(main_1_out_2_2[4]));
  _7_Segment_Display u_7_segment_display_2 (
    .g(main_1_out_2[3]), .f(main_1_out_2[2]), .a(main_1_out_2[1]), .b(main_1_out_2[0]),
    .e(main_1_out_2_2[3]), .d(main_1_out_2_2[2]), .c(main_1_out_2_2[1]), .dp(main_1_out_2_2[0]));
  display_driver2_main main_1 (.out_2({main_1_out_2_2, main_1_out_2}), .in_1(A_2));
  LED led_1 (.in(rom_1_data[31]));
  Button button_1 (.out(button_1_out));
  not not_1 (not_1_out, button_1_out);
  Clock clock_1 (.out(clock_1_out));
  Button button_2 (.out(button_2_out));
  _7_Segment_Display u_7_segment_display_3 (
    .g(main_2_out_2[7]), .f(main_2_out_2[6]), .a(main_2_out_2[5]), .b(main_2_out_2[4]),
    .e(main_2_out_2_2[7]), .d(main_2_out_2_2[6]), .c(main_2_out_2_2[5]), .dp(main_2_out_2_2[4]));
  _7_Segment_Display u_7_segment_display_4 (
    .g(main_2_out_2[3]), .f(main_2_out_2[2]), .a(main_2_out_2[1]), .b(main_2_out_2[0]),
    .e(main_2_out_2_2[3]), .d(main_2_out_2_2[2]), .c(main_2_out_2_2[1]), .dp(main_2_out_2_2[0]));
  and and_1 (and_1_out, rom_1_data[31], and_2_out);
  and and_2 (and_2_out, not_1_out, in_1);
  or or_1 (or_1_out, and_1_out, clock_1_out);
  _7_Segment_Display u_7_segment_display_5 (
    .g(main_4_out_2[7]), .f(main_4_out_2[6]), .a(main_4_out_2[5]), .b(main_4_out_2[4]),
    .e(main_4_out_2_2[7]), .d(main_4_out_2_2[6]), .c(main_4_out_2_2[5]), .dp(main_4_out_2_2[4]));
  display_driver2_main main_2 (.out_2({main_2_out_2_2, main_2_out_2}), .in_1(B_2));
  and and_3 (and_3_out, in_1, main_6_halt);
  program_counter_main main_3 (
    .in_7(button_2_out), .in_8(or_1_out), .out_9(out_5[5]), .out_10(out_5[4]), .out_11(out_5[3]),
    .out_12(out_5[2]), .out_13(out_5[1]), .out_14(out_5[0]), .in_1(and_4_out), .in_2(and_5_out),
    .in_3(and_6_out), .in_4(and_7_out), .in_5(and_8_out), .in_6(and_10_out));
  _7_Segment_Display u_7_segment_display_6 (
    .g(main_4_out_2[3]), .f(main_4_out_2[2]), .a(main_4_out_2[1]), .b(main_4_out_2[0]),
    .e(main_4_out_2_2[3]), .d(main_4_out_2_2[2]), .c(main_4_out_2_2[1]), .dp(main_4_out_2_2[0]));
  display_driver2_main main_4 (.out_2({main_4_out_2_2, main_4_out_2}), .in_1(C_2));
  and and_4 (and_4_out, in_1, and_15_out[5]);
  _7_Segment_Display u_7_segment_display_7 (
    .g(main_5_out_2[7]), .f(main_5_out_2[6]), .a(main_5_out_2[5]), .b(main_5_out_2[4]),
    .e(main_5_out_2_2[7]), .d(main_5_out_2_2[6]), .c(main_5_out_2_2[5]), .dp(main_5_out_2_2[4]));
  and and_5 (and_5_out, in_1, and_15_out[4]);
  _7_Segment_Display u_7_segment_display_8 (
    .g(main_5_out_2[3]), .f(main_5_out_2[2]), .a(main_5_out_2[1]), .b(main_5_out_2[0]),
    .e(main_5_out_2_2[3]), .d(main_5_out_2_2[2]), .c(main_5_out_2_2[1]), .dp(main_5_out_2_2[0]));
  display_driver2_main main_5 (.out_2({main_5_out_2_2, main_5_out_2}), .in_1(A));
  instructor_main main_6 (
    .in_1(rom_1_data[30]), .in_2(rom_1_data[29]), .in_3(rom_1_data[28]), .in_4(rom_1_data[27]),
    .ADD(main_6_add), .INVERT(main_6_invert), .A_B(main_6_a_b), .A_B_2(main_6_a_b_2), .A_B_3(main_6_a_b_3),
    .STEP(main_6_step), .INSERT(main_6_insert), .OUT(main_6_out), .HALT(main_6_halt), .out_14(main_6_out_14),
    .out_15(main_6_out_15), .out_16(main_6_out_16), .out_17(main_6_out_17));  // open: out_18, out_19
  and and_6 (and_6_out, in_1, and_15_out[3]);
  _7_Segment_Display u_7_segment_display_9 (
    .g(main_7_out_2[3]), .f(main_7_out_2[2]), .a(main_7_out_2[1]), .b(main_7_out_2[0]),
    .e(main_7_out_2_2[3]), .d(main_7_out_2_2[2]), .c(main_7_out_2_2[1]), .dp(main_7_out_2_2[0]));
  _7_Segment_Display u_7_segment_display_10 (
    .g(main_7_out_2[7]), .f(main_7_out_2[6]), .a(main_7_out_2[5]), .b(main_7_out_2[4]),
    .e(main_7_out_2_2[7]), .d(main_7_out_2_2[6]), .c(main_7_out_2_2[5]), .dp(main_7_out_2_2[4]));
  display_driver2_main main_7 (.out_2({main_7_out_2_2, main_7_out_2}), .in_1(B));
  or_operator_main main_8 (.in_1(main_20_out_23), .in_2(main_21_out_23), .out_3(main_8_out_3));
  and_operator_main main_9 (.in_1(main_20_out_23), .in_2(main_21_out_23), .out_3(main_9_out_3));
  bitshifter_main main_10 (.in_1(main_20_out_23), .in_2(main_21_out_23), .out_3(main_10_out_3));
  step_selector_main main_11 (
    .in_2(main_22_out_23[0]), .in_1(main_20_out_23), .in_3(main_21_out_23), .out_4(main_11_out_4));
  equality_check_main main_12 (
    .Equality_Check(main_12_equality_check[0]), .in_1(main_20_out_23[5]), .in_2(main_20_out_23[4]),
    .Number_A(main_20_out_23[3]), .in_4(main_20_out_23[2]), .in_5(main_20_out_23[1]),
    .in_6(main_20_out_23[0]), .in_7(main_21_out_23[5]), .in_8(main_21_out_23[4]), .in_9(main_21_out_23[3]),
    .in_10(main_21_out_23[2]), .in_11(main_21_out_23[1]), .in_12(main_21_out_23[0]));
  a_less_than_b_main main_13 (
    .in_7(main_21_out_23[5]), .in_8(main_21_out_23[4]), .in_9(main_21_out_23[3]), .in_10(main_21_out_23[2]),
    .in_11(main_21_out_23[1]), .in_12(main_21_out_23[0]), .in_1(main_20_out_23[5]), .in_2(main_20_out_23[4]),
    .in_3(main_20_out_23[3]), .in_4(main_20_out_23[2]), .in_5(main_20_out_23[1]), .in_6(main_20_out_23[0]),
    .out_13(main_13_out_13[0]));
  a_greater_than_b_main main_14 (
    .in_1(main_20_out_23[5]), .in_2(main_20_out_23[4]), .in_3(main_20_out_23[3]), .in_4(main_20_out_23[2]),
    .in_5(main_20_out_23[1]), .in_6(main_20_out_23[0]), .in_7(main_21_out_23[5]), .in_8(main_21_out_23[4]),
    .in_9(main_21_out_23[3]), .in_10(main_21_out_23[2]), .in_11(main_21_out_23[1]),
    .in_12(main_21_out_23[0]), .out_13(main_14_out_13[0]));
  inverter_main main_15 (
    .in_1(main_20_out_23[5]), .in_2(main_20_out_23[4]), .in_3(main_20_out_23[3]), .in_4(main_20_out_23[2]),
    .in_5(main_20_out_23[1]), .in_6(main_20_out_23[0]), .out_7(main_15_out_12[5]), .out_8(main_15_out_12[4]),
    .out_9(main_15_out_12[3]), .out_10(main_15_out_12[2]), .out_11(main_15_out_12[1]),
    .out_12(main_15_out_12[0]));
  input_selector_main main_16 (
    .in_4(main_6_out), .in_1({6{1'b0}}), .in_2({6{1'b0}}), .in_3({6{1'b0}}), .in_5(main_20_out_23),
    .in_6(main_21_out_23), .in_7(main_22_out_23), .out_8(A_2), .out_9(B_2), .out_10(C_2));
  and and_7 (and_7_out, in_1, and_15_out[2]);
  _7_Segment_Display u_7_segment_display_11 (
    .g(main_18_out_2[7]), .f(main_18_out_2[6]), .a(main_18_out_2[5]), .b(main_18_out_2[4]),
    .e(main_18_out_2_2[7]), .d(main_18_out_2_2[6]), .c(main_18_out_2_2[5]), .dp(main_18_out_2_2[4]));
  addition_main main_17 (
    .in_1(main_21_out_23[5]), .in_2(main_21_out_23[4]), .in_3(main_21_out_23[3]), .in_4(main_21_out_23[2]),
    .in_5(main_21_out_23[1]), .in_6(main_21_out_23[0]), .in_7(main_20_out_23[5]), .in_8(main_20_out_23[4]),
    .in_9(main_20_out_23[3]), .in_10(main_20_out_23[2]), .in_11(main_20_out_23[1]),
    .in_12(main_20_out_23[0]), .out_14(main_17_out_19[5]), .out_15(main_17_out_19[4]),
    .out_16(main_17_out_19[3]), .out_17(main_17_out_19[2]), .out_18(main_17_out_19[1]),
    .out_19(main_17_out_19[0]));  // open: out_13
  ROM #(.addrWidth(6), .dataWidth(32)) rom_1 (.addr(out_5), .data(rom_1_data));  // open: sel
  and and_8 (and_8_out, in_1, and_15_out[1]);
  _7_Segment_Display u_7_segment_display_12 (
    .g(main_18_out_2[3]), .f(main_18_out_2[2]), .a(main_18_out_2[1]), .b(main_18_out_2[0]),
    .e(main_18_out_2_2[3]), .d(main_18_out_2_2[2]), .c(main_18_out_2_2[1]), .dp(main_18_out_2_2[0]));
  display_driver2_main main_18 (.out_2({main_18_out_2_2, main_18_out_2}), .in_1(C));
  value_transfer_main main_19 (
    .Inp_A(main_20_out_23), .Inp_C(main_22_out_23), .Inp_B(main_21_out_23), .To_B(main_19_to_b),
    .To_A(main_19_to_a), .To_C(main_19_to_c));
  and and_9 (and_15_out[5], main_11_out_4[5], main_6_step);
  memory_small_clocked_main main_20 (
    .Address(rom_1_data[23]), .in_6(rom_1_data[22]), .Write(rom_1_data[21]), .in_8(rom_1_data[20]),
    .Read(rom_1_data[19]), .Initialise(button_2_out), .in_12(main_33_out_8[5]), .in_13(main_33_out_8[4]),
    .Input(main_33_out_8[3]), .in_15(main_33_out_8[2]), .in_16(main_33_out_8[1]), .in_17(main_33_out_8[0]),
    .out_18(main_20_out_23[5]), .out_19(main_20_out_23[4]), .Output(main_20_out_23[3]),
    .out_21(main_20_out_23[2]), .out_22(main_20_out_23[1]), .out_23(main_20_out_23[0]),
    .in_4(rom_1_data[24]), .Alt(rom_1_data[25]), .in_2(rom_1_data[26]), .Pass(rom_1_data[18]), .Clk(or_1_out));
  and and_10 (and_10_out, in_1, and_15_out[0]);
  and and_11 (and_15_out[4], main_11_out_4[4], main_6_step);
  and and_12 (and_15_out[3], main_11_out_4[3], main_6_step);
  and and_13 (and_15_out[2], main_11_out_4[2], main_6_step);
  memory_small_clocked_main main_21 (
    .Address(rom_1_data[14]), .in_6(rom_1_data[13]), .Write(rom_1_data[12]), .in_8(rom_1_data[11]),
    .Read(rom_1_data[10]), .Initialise(button_2_out), .in_12(main_33_out_9[5]), .in_13(main_33_out_9[4]),
    .Input(main_33_out_9[3]), .in_15(main_33_out_9[2]), .in_16(main_33_out_9[1]), .in_17(main_33_out_9[0]),
    .out_18(main_21_out_23[5]), .out_19(main_21_out_23[4]), .Output(main_21_out_23[3]),
    .out_21(main_21_out_23[2]), .out_22(main_21_out_23[1]), .out_23(main_21_out_23[0]),
    .in_4(rom_1_data[15]), .Alt(rom_1_data[16]), .in_2(rom_1_data[17]), .Pass(rom_1_data[9]), .Clk(or_1_out));
  and and_14 (and_15_out[1], main_11_out_4[1], main_6_step);
  and and_15 (and_15_out[0], main_11_out_4[0], main_6_step);
  memory_small_clocked_main main_22 (
    .Address(rom_1_data[5]), .in_6(rom_1_data[4]), .Write(rom_1_data[3]), .in_8(rom_1_data[2]),
    .Read(rom_1_data[1]), .Initialise(button_2_out), .in_12(main_33_out_10[5]), .in_13(main_33_out_10[4]),
    .Input(main_33_out_10[3]), .in_15(main_33_out_10[2]), .in_16(main_33_out_10[1]),
    .in_17(main_33_out_10[0]), .out_18(main_22_out_23[5]), .out_19(main_22_out_23[4]),
    .Output(main_22_out_23[3]), .out_21(main_22_out_23[2]), .out_22(main_22_out_23[1]),
    .out_23(main_22_out_23[0]), .in_4(rom_1_data[6]), .Alt(rom_1_data[7]), .in_2(rom_1_data[8]),
    .Pass(rom_1_data[0]), .Clk(or_1_out));
  input_selector_main main_23 (
    .in_4(main_6_out_17), .in_1({6{1'b0}}), .in_2({6{1'b0}}), .in_3({6{1'b0}}), .in_5({6{1'b0}}),
    .in_6({6{1'b0}}), .in_7(main_8_out_3), .out_8(main_23_out_8), .out_9(main_23_out_9),
    .out_10(main_23_out_10));
  input_selector_main main_24 (
    .in_4(main_6_out_16), .in_1(main_23_out_8), .in_2(main_23_out_9), .in_3(main_23_out_10),
    .in_5({6{1'b0}}), .in_6({6{1'b0}}), .in_7(main_9_out_3), .out_8(main_24_out_8), .out_9(main_24_out_9),
    .out_10(main_24_out_10));
  input_selector_main main_25 (
    .in_4(main_6_out_15), .in_1(main_24_out_8), .in_2(main_24_out_9), .in_3(main_24_out_10), .in_5(out_5),
    .in_6(out_5), .in_7(out_5), .out_8(main_25_out_8), .out_9(main_25_out_9), .out_10(main_25_out_10));
  input_selector_main main_26 (
    .in_4(main_6_out_14), .in_1(main_25_out_8), .in_2(main_25_out_9), .in_3(main_25_out_10),
    .in_5({6{1'b0}}), .in_6({6{1'b0}}), .in_7(main_10_out_3), .out_8(main_26_out_8), .out_9(main_26_out_9),
    .out_10(main_26_out_10));
  input_selector_main main_27 (
    .in_4(and_3_out), .in_1(main_26_out_8), .in_2(main_26_out_9), .in_3(main_26_out_10), .in_5(main_19_to_a),
    .in_6(main_19_to_b), .in_7(main_19_to_c), .out_8(main_27_out_8), .out_9(main_27_out_9),
    .out_10(main_27_out_10));
  input_selector_main main_28 (
    .in_4(main_6_a_b_3), .in_1(main_27_out_8), .in_2(main_27_out_9), .in_3(main_27_out_10), .in_5({6{1'b0}}),
    .in_6({6{1'b0}}), .in_7({{5{1'b0}}, main_12_equality_check[0]}), .out_8(main_28_out_8),
    .out_9(main_28_out_9), .out_10(main_28_out_10));
  input_selector_main main_29 (
    .in_4(main_6_a_b_2), .in_1(main_28_out_8), .in_2(main_28_out_9), .in_3(main_28_out_10), .in_5({6{1'b0}}),
    .in_6({6{1'b0}}), .in_7({{5{1'b0}}, main_13_out_13[0]}), .out_8(main_29_out_8), .out_9(main_29_out_9),
    .out_10(main_29_out_10));
  input_selector_main main_30 (
    .in_4(main_6_a_b), .in_1(main_29_out_8), .in_2(main_29_out_9), .in_3(main_29_out_10), .in_5({6{1'b0}}),
    .in_6({6{1'b0}}), .in_7({{5{1'b0}}, main_14_out_13[0]}), .out_8(main_30_out_8), .out_9(main_30_out_9),
    .out_10(main_30_out_10));
  input_selector_main main_31 (
    .in_4(main_6_invert), .in_1(main_30_out_8), .in_2(main_30_out_9), .in_3(main_30_out_10),
    .in_5({6{1'b0}}), .in_6({6{1'b0}}), .in_7(main_15_out_12), .out_8(main_31_out_8), .out_9(main_31_out_9),
    .out_10(main_31_out_10));
  input_selector_main main_32 (
    .in_4(main_6_insert), .in_1(main_31_out_8), .in_2(main_31_out_9), .in_3(main_31_out_10), .in_5(A),
    .in_6(B), .in_7(C), .out_8(main_32_out_8), .out_9(main_32_out_9), .out_10(main_32_out_10));
  input_selector_main main_33 (
    .in_4(main_6_add), .in_1(main_32_out_8), .in_2(main_32_out_9), .in_3(main_32_out_10), .in_5({6{1'b0}}),
    .in_6({6{1'b0}}), .in_7(main_17_out_19), .out_8(main_33_out_8), .out_9(main_33_out_9),
    .out_10(main_33_out_10));

  // Notes on the sheet:
  //   Go
  //   Clock
  //   Counter
  //   Initialise
  //   Set value to 1 after initialization
  //   Output
  //   Input
  //   contents of rom_1 (hex, n*v repeats v):
  //   0 b8301800 48282800 48501200 828240c 4830000a 8481214 48500012 2848141c 3084a21a c000000a
endmodule
