// Logisim project select input output bus.circ as structural Verilog: 1 circuit, main circuit main
module main (
  input  in_1,
  input  in_2,
  input  in_3,
  input  in_4,
  input  in_5,
  input  in_6,
  input  in_7,
  input  in_8,
  input  in_9,
  input  in_10,
  input  in_11,
  input  in_12,
  input  in_13,
  input  in_14,
  input  in_15,
  input  in_16,
  input  in_17,
  input  in_18,
  input  in_19,
  input  in_20,
  input  in_21,
  input  in_22,
  input  in_23,
  input  in_24,
  input  in_25,
  input  in_26,
  input  in_27,
  input  in_28,
  input  in_29,
  input  in_30,
  input  in_31,
  input  in_32,
  input  in_33,
  input  in_34,
  input  in_35,
  input  in_36,
  input  in_37,
  output out_38,
  output out_39,
  output out_40,
  output out_41,
  output out_42,
  output out_43,
  output out_44,
  output out_45,
  output out_46,
  output out_47,
  output out_48,
  output out_49,
  output out_50,
  output out_51,
  output out_52,
  output out_53,
  output out_54,
  output out_55
);

  wire and_1_out, and_2_out, and_3_out, and_4_out, and_5_out, and_6_out, and_7_out, and_8_out, and_9_out,
       and_10_out, and_11_out, and_12_out, and_13_out, and_14_out, and_15_out, and_16_out, and_17_out,
       and_18_out, and_19_out, and_20_out, and_21_out, and_22_out, and_23_out, and_24_out, and_25_out,
       and_26_out, and_27_out, and_28_out, and_29_out, and_30_out, and_31_out, and_32_out, and_33_out,
       and_34_out, and_35_out, and_36_out, not_1_out;

  not not_1 (not_1_out, in_19);
  and and_1 (and_1_out, in_1, not_1_out);
  and and_2 (and_2_out, in_19, in_20);
  and and_3 (and_3_out, in_2, not_1_out);
  or or_1 (out_38, and_1_out, and_2_out);
  and and_4 (and_4_out, in_19, in_21);
  and and_5 (and_5_out, in_3, not_1_out);
  or or_2 (out_39, and_3_out, and_4_out);
  and and_6 (and_6_out, in_19, in_22);
  or or_3 (out_40, and_5_out, and_6_out);
  and and_7 (and_7_out, in_4, not_1_out);
  and and_8 (and_8_out, in_19, in_23);
  and and_9 (and_9_out, in_5, not_1_out);
  or or_4 (out_41, and_7_out, and_8_out);
  and and_10 (and_10_out, in_19, in_24);
  and and_11 (and_11_out, in_6, not_1_out);
  or or_5 (out_42, and_9_out, and_10_out);
  and and_12 (and_12_out, in_19, in_25);
  or or_6 (out_43, and_11_out, and_12_out);
  and and_13 (and_13_out, in_7, not_1_out);
  and and_14 (and_14_out, in_19, in_26);
  and and_15 (and_15_out, in_8, not_1_out);
  or or_7 (out_44, and_13_out, and_14_out);
  and and_16 (and_16_out, in_19, in_27);
  and and_17 (and_17_out, in_9, not_1_out);
  or or_8 (out_45, and_15_out, and_16_out);
  and and_18 (and_18_out, in_19, in_28);
  and and_19 (and_19_out, in_10, not_1_out);
  or or_9 (out_46, and_17_out, and_18_out);
  and and_20 (and_20_out, in_19, in_29);
  and and_21 (and_21_out, in_11, not_1_out);
  or or_10 (out_47, and_19_out, and_20_out);
  and and_22 (and_22_out, in_19, in_30);
  or or_11 (out_48, and_21_out, and_22_out);
  and and_23 (and_23_out, in_12, not_1_out);
  and and_24 (and_24_out, in_19, in_31);
  and and_25 (and_25_out, in_13, not_1_out);
  or or_12 (out_49, and_23_out, and_24_out);
  and and_26 (and_26_out, in_19, in_32);
  and and_27 (and_27_out, in_14, not_1_out);
  or or_13 (out_50, and_25_out, and_26_out);
  and and_28 (and_28_out, in_19, in_33);
  or or_14 (out_51, and_27_out, and_28_out);
  and and_29 (and_29_out, in_15, not_1_out);
  and and_30 (and_30_out, in_19, in_34);
  and and_31 (and_31_out, in_16, not_1_out);
  or or_15 (out_52, and_29_out, and_30_out);
  and and_32 (and_32_out, in_19, in_35);
  and and_33 (and_33_out, in_17, not_1_out);
  or or_16 (out_53, and_31_out, and_32_out);
  and and_34 (and_34_out, in_19, in_36);
  and and_35 (and_35_out, in_18, not_1_out);
  or or_17 (out_54, and_33_out, and_34_out);
  and and_36 (and_36_out, in_19, in_37);
  or or_18 (out_55, and_35_out, and_36_out);
endmodule
