// Logisim project seven segment display step counter.circ as structural Verilog: 1 circuit, main circuit main
module main (
  input  in_1,
  input  in_2,
  input  in_3,
  input  in_4
);

  wire and_1_out, and_2_out, and_3_out, and_4_out, and_5_out, and_6_out, and_7_out, and_8_out, and_9_out,
       and_10_out, and_11_out, and_12_out, and_13_out, and_14_out, and_15_out, and_16_out, and_17_out,
       and_18_out, and_19_out, and_20_out, and_21_out, and_22_out, and_23_out, and_24_out, and_25_out,
       and_26_out, and_27_out, and_28_out, and_29_out, and_30_out, and_31_out, and_32_out, and_33_out,
       and_34_out, and_35_out, and_36_out, and_37_out, and_38_out, and_39_out, and_40_out, and_41_out,
       and_42_out, and_43_out, and_44_out, and_45_out, and_46_out, and_47_out, and_48_out, and_49_out,
       and_50_out, and_51_out, and_52_out, and_53_out, and_54_out, and_55_out, and_56_out, and_57_out,
       and_58_out, and_59_out, and_60_out, and_61_out, and_62_out, and_63_out, and_64_out, and_65_out,
       and_66_out, and_67_out, and_68_out, and_69_out, and_70_out, and_71_out, and_72_out, and_73_out,
       and_74_out, and_75_out, and_76_out, and_77_out, and_78_out, and_79_out, and_80_out, and_81_out,
       and_82_out, and_83_out, and_84_out, and_85_out, and_86_out, and_87_out, and_88_out, and_89_out,
       and_90_out, and_91_out, and_92_out, and_93_out, and_94_out, and_95_out, and_96_out, and_97_out,
       and_98_out, and_99_out, and_100_out, and_101_out, and_102_out, and_103_out, and_104_out, and_105_out,
       and_106_out, and_107_out, and_108_out, and_109_out, and_110_out, or_1_out, or_2_out, or_3_out,
       or_4_out, or_5_out, or_6_out, or_7_out, or_8_out, or_9_out, or_10_out, or_11_out, or_12_out,
       or_13_out, or_14_out, or_15_out, or_16_out, or_17_out, or_18_out, or_19_out, or_20_out, or_21_out,
       or_22_out, or_23_out, or_24_out, or_25_out, or_26_out, or_27_out, or_28_out, or_29_out, or_30_out,
       or_31_out, or_32_out, or_33_out, or_34_out, or_35_out, or_36_out, or_37_out, or_38_out, or_39_out,
       or_40_out, or_41_out, or_42_out, or_43_out, or_44_out, or_45_out, or_46_out, or_47_out, or_48_out,
       or_49_out, or_50_out, or_51_out, or_52_out, or_53_out, or_54_out, or_55_out, or_56_out, or_57_out,
       or_58_out, or_59_out, or_60_out, or_61_out, or_62_out, or_63_out, or_64_out, or_65_out, or_66_out,
       or_67_out, or_68_out, or_69_out, or_70_out, or_71_out, or_72_out, xnor_1_out, xnor_2_out, xnor_3_out,
       xnor_4_out, xnor_5_out, xnor_6_out, xnor_7_out, xnor_8_out, xnor_9_out, xnor_10_out, xnor_11_out,
       xnor_12_out, xnor_13_out, xnor_14_out, xnor_15_out, xnor_16_out, xnor_17_out, xnor_18_out,
       xnor_19_out, xnor_20_out, xnor_21_out, xnor_22_out, xnor_23_out, xnor_24_out, xnor_25_out,
       xnor_26_out, xnor_27_out, xnor_28_out, xnor_29_out, xnor_30_out, xnor_31_out, xnor_32_out,
       xnor_33_out, xnor_34_out, xnor_35_out, xnor_36_out, xnor_37_out, xnor_38_out, xnor_39_out, xnor_40_out;

  _7_Segment_Display u_7_segment_display_1 (
    .g(or_37_out), .f(or_46_out), .a(or_55_out), .b(or_64_out), .e(or_28_out), .d(or_19_out), .c(or_10_out),
    .dp(or_1_out));
  xnor xnor_1 (xnor_1_out, 1'b0, in_4);
  xnor xnor_2 (xnor_2_out, 1'b0, in_3);
  xnor xnor_3 (xnor_3_out, 1'b0, in_2);
  xnor xnor_4 (xnor_4_out, 1'b0, in_1);
  xnor xnor_5 (xnor_5_out, 1'b1, in_4);
  xnor xnor_6 (xnor_6_out, 1'b0, in_3);
  xnor xnor_7 (xnor_7_out, 1'b0, in_2);
  xnor xnor_8 (xnor_8_out, 1'b0, in_1);
  xnor xnor_9 (xnor_9_out, 1'b0, in_4);
  xnor xnor_10 (xnor_10_out, 1'b1, in_3);
  xnor xnor_11 (xnor_11_out, 1'b0, in_2);
  xnor xnor_12 (xnor_12_out, 1'b0, in_1);
  xnor xnor_13 (xnor_13_out, 1'b1, in_4);
  xnor xnor_14 (xnor_14_out, 1'b1, in_3);
  xnor xnor_15 (xnor_15_out, 1'b0, in_2);
  xnor xnor_16 (xnor_16_out, 1'b0, in_1);
  xnor xnor_17 (xnor_17_out, 1'b0, in_4);
  xnor xnor_18 (xnor_18_out, 1'b0, in_3);
  xnor xnor_19 (xnor_19_out, 1'b1, in_2);
  xnor xnor_20 (xnor_20_out, 1'b0, in_1);
  xnor xnor_21 (xnor_21_out, 1'b1, in_4);
  xnor xnor_22 (xnor_22_out, 1'b0, in_3);
  xnor xnor_23 (xnor_23_out, 1'b1, in_2);
  xnor xnor_24 (xnor_24_out, 1'b0, in_1);
  xnor xnor_25 (xnor_25_out, 1'b0, in_4);
  xnor xnor_26 (xnor_26_out, 1'b1, in_3);
  xnor xnor_27 (xnor_27_out, 1'b1, in_2);
  xnor xnor_28 (xnor_28_out, 1'b0, in_1);
  xnor xnor_29 (xnor_29_out, 1'b1, in_4);
  xnor xnor_30 (xnor_30_out, 1'b1, in_3);
  xnor xnor_31 (xnor_31_out, 1'b1, in_2);
  xnor xnor_32 (xnor_32_out, 1'b0, in_1);
  xnor xnor_33 (xnor_33_out, 1'b0, in_4);
  xnor xnor_34 (xnor_34_out, 1'b0, in_3);
  xnor xnor_35 (xnor_35_out, 1'b0, in_2);
  xnor xnor_36 (xnor_36_out, 1'b1, in_1);
  xnor xnor_37 (xnor_37_out, 1'b1, in_4);
  xnor xnor_38 (xnor_38_out, 1'b0, in_3);
  xnor xnor_39 (xnor_39_out, 1'b0, in_2);
  xnor xnor_40 (xnor_40_out, 1'b1, in_1);
  and and_1 (and_1_out, xnor_1_out, xnor_2_out);
  and and_2 (and_2_out, and_1_out, xnor_3_out);
  and and_3 (and_3_out, xnor_5_out, xnor_6_out);
  and and_4 (and_4_out, and_3_out, xnor_7_out);
  and and_5 (and_5_out, xnor_9_out, xnor_10_out);
  and and_6 (and_6_out, and_5_out, xnor_11_out);
  and and_7 (and_7_out, xnor_13_out, xnor_14_out);
  and and_8 (and_8_out, and_7_out, xnor_15_out);
  and and_9 (and_9_out, xnor_17_out, xnor_18_out);
  and and_10 (and_10_out, and_9_out, xnor_19_out);
  and and_11 (and_11_out, xnor_21_out, xnor_22_out);
  and and_12 (and_12_out, and_11_out, xnor_23_out);
  and and_13 (and_13_out, xnor_25_out, xnor_26_out);
  and and_14 (and_14_out, and_13_out, xnor_27_out);
  and and_15 (and_15_out, xnor_29_out, xnor_30_out);
  and and_16 (and_16_out, and_15_out, xnor_31_out);
  and and_17 (and_17_out, xnor_33_out, xnor_34_out);
  and and_18 (and_18_out, and_17_out, xnor_35_out);
  and and_19 (and_19_out, xnor_37_out, xnor_38_out);
  and and_20 (and_20_out, and_19_out, xnor_39_out);
  and and_21 (and_21_out, and_2_out, xnor_4_out);
  and and_22 (and_22_out, and_4_out, xnor_8_out);
  and and_23 (and_23_out, and_6_out, xnor_12_out);
  and and_24 (and_24_out, and_8_out, xnor_16_out);
  and and_25 (and_25_out, and_10_out, xnor_20_out);
  and and_26 (and_26_out, and_12_out, xnor_24_out);
  and and_27 (and_27_out, and_14_out, xnor_28_out);
  and and_28 (and_28_out, and_16_out, xnor_32_out);
  and and_29 (and_29_out, and_18_out, xnor_36_out);
  and and_30 (and_30_out, and_20_out, xnor_40_out);
  and and_31 (and_31_out, 1'b1, and_21_out);
  and and_32 (and_32_out, 1'b1, and_21_out);
  and and_33 (and_33_out, 1'b1, and_21_out);
  and and_34 (and_34_out, 1'b0, and_21_out);
  and and_35 (and_35_out, 1'b1, and_21_out);
  and and_36 (and_36_out, 1'b1, and_21_out);
  and and_37 (and_37_out, 1'b1, and_21_out);
  and and_38 (and_38_out, 1'b0, and_21_out);
  and and_39 (and_39_out, 1'b1, and_22_out);
  and and_40 (and_40_out, 1'b0, and_22_out);
  and and_41 (and_41_out, 1'b0, and_22_out);
  and and_42 (and_42_out, 1'b0, and_22_out);
  and and_43 (and_43_out, 1'b0, and_22_out);
  and and_44 (and_44_out, 1'b0, and_22_out);
  and and_45 (and_45_out, 1'b1, and_22_out);
  and and_46 (and_46_out, 1'b0, and_22_out);
  and and_47 (and_47_out, 1'b1, and_23_out);
  and and_48 (and_48_out, 1'b1, and_23_out);
  and and_49 (and_49_out, 1'b0, and_23_out);
  and and_50 (and_50_out, 1'b1, and_23_out);
  and and_51 (and_51_out, 1'b1, and_23_out);
  and and_52 (and_52_out, 1'b1, and_23_out);
  and and_53 (and_53_out, 1'b0, and_23_out);
  and and_54 (and_54_out, 1'b0, and_23_out);
  and and_55 (and_55_out, 1'b1, and_24_out);
  and and_56 (and_56_out, 1'b1, and_24_out);
  and and_57 (and_57_out, 1'b0, and_24_out);
  and and_58 (and_58_out, 1'b1, and_24_out);
  and and_59 (and_59_out, 1'b0, and_24_out);
  and and_60 (and_60_out, 1'b1, and_24_out);
  and and_61 (and_61_out, 1'b1, and_24_out);
  and and_62 (and_62_out, 1'b0, and_24_out);
  and and_63 (and_63_out, 1'b1, and_25_out);
  and and_64 (and_64_out, 1'b0, and_25_out);
  and and_65 (and_65_out, 1'b1, and_25_out);
  and and_66 (and_66_out, 1'b1, and_25_out);
  and and_67 (and_67_out, 1'b0, and_25_out);
  and and_68 (and_68_out, 1'b0, and_25_out);
  and and_69 (and_69_out, 1'b1, and_25_out);
  and and_70 (and_70_out, 1'b0, and_25_out);
  and and_71 (and_71_out, 1'b0, and_26_out);
  and and_72 (and_72_out, 1'b1, and_26_out);
  and and_73 (and_73_out, 1'b1, and_26_out);
  and and_74 (and_74_out, 1'b1, and_26_out);
  and and_75 (and_75_out, 1'b0, and_26_out);
  and and_76 (and_76_out, 1'b1, and_26_out);
  and and_77 (and_77_out, 1'b1, and_26_out);
  and and_78 (and_78_out, 1'b0, and_26_out);
  and and_79 (and_79_out, 1'b0, and_27_out);
  and and_80 (and_80_out, 1'b1, and_27_out);
  and and_81 (and_81_out, 1'b1, and_27_out);
  and and_82 (and_82_out, 1'b1, and_27_out);
  and and_83 (and_83_out, 1'b1, and_27_out);
  and and_84 (and_84_out, 1'b1, and_27_out);
  and and_85 (and_85_out, 1'b1, and_27_out);
  and and_86 (and_86_out, 1'b0, and_27_out);
  and and_87 (and_87_out, 1'b1, and_28_out);
  and and_88 (and_88_out, 1'b1, and_28_out);
  and and_89 (and_89_out, 1'b0, and_28_out);
  and and_90 (and_90_out, 1'b0, and_28_out);
  and and_91 (and_91_out, 1'b0, and_28_out);
  and and_92 (and_92_out, 1'b0, and_28_out);
  and and_93 (and_93_out, 1'b1, and_28_out);
  and and_94 (and_94_out, 1'b0, and_28_out);
  and and_95 (and_95_out, 1'b1, and_29_out);
  and and_96 (and_96_out, 1'b1, and_29_out);
  and and_97 (and_97_out, 1'b1, and_29_out);
  and and_98 (and_98_out, 1'b1, and_29_out);
  and and_99 (and_99_out, 1'b1, and_29_out);
  and and_100 (and_100_out, 1'b1, and_29_out);
  and and_101 (and_101_out, 1'b1, and_29_out);
  and and_102 (and_102_out, 1'b0, and_29_out);
  and and_103 (and_103_out, 1'b1, and_30_out);
  and and_104 (and_104_out, 1'b1, and_30_out);
  and and_105 (and_105_out, 1'b1, and_30_out);
  and and_106 (and_106_out, 1'b1, and_30_out);
  and and_107 (and_107_out, 1'b0, and_30_out);
  and and_108 (and_108_out, 1'b1, and_30_out);
  and and_109 (and_109_out, 1'b1, and_30_out);
  and and_110 (and_110_out, 1'b0, and_30_out);
  or or_1 (or_1_out, and_38_out, or_2_out);
  or or_2 (or_2_out, and_46_out, or_3_out);
  or or_3 (or_3_out, and_54_out, or_4_out);
  or or_4 (or_4_out, and_62_out, or_5_out);
  or or_5 (or_5_out, and_70_out, or_6_out);
  or or_6 (or_6_out, and_78_out, or_7_out);
  or or_7 (or_7_out, and_86_out, or_8_out);
  or or_8 (or_8_out, and_94_out, or_9_out);
  or or_9 (or_9_out, and_102_out, and_110_out);
  or or_10 (or_10_out, and_37_out, or_11_out);
  or or_11 (or_11_out, and_45_out, or_12_out);
  or or_12 (or_12_out, and_53_out, or_13_out);
  or or_13 (or_13_out, and_61_out, or_14_out);
  or or_14 (or_14_out, and_69_out, or_15_out);
  or or_15 (or_15_out, and_77_out, or_16_out);
  or or_16 (or_16_out, and_85_out, or_17_out);
  or or_17 (or_17_out, and_93_out, or_18_out);
  or or_18 (or_18_out, and_101_out, and_109_out);
  or or_19 (or_19_out, and_36_out, or_20_out);
  or or_20 (or_20_out, and_44_out, or_21_out);
  or or_21 (or_21_out, and_52_out, or_22_out);
  or or_22 (or_22_out, and_60_out, or_23_out);
  or or_23 (or_23_out, and_68_out, or_24_out);
  or or_24 (or_24_out, and_76_out, or_25_out);
  or or_25 (or_25_out, and_84_out, or_26_out);
  or or_26 (or_26_out, and_92_out, or_27_out);
  or or_27 (or_27_out, and_100_out, and_108_out);
  or or_28 (or_28_out, and_35_out, or_29_out);
  or or_29 (or_29_out, and_43_out, or_30_out);
  or or_30 (or_30_out, and_51_out, or_31_out);
  or or_31 (or_31_out, and_59_out, or_32_out);
  or or_32 (or_32_out, and_67_out, or_33_out);
  or or_33 (or_33_out, and_75_out, or_34_out);
  or or_34 (or_34_out, and_83_out, or_35_out);
  or or_35 (or_35_out, and_91_out, or_36_out);
  or or_36 (or_36_out, and_99_out, and_107_out);
  or or_37 (or_37_out, and_34_out, or_38_out);
  or or_38 (or_38_out, and_42_out, or_39_out);
  or or_39 (or_39_out, and_50_out, or_40_out);
  or or_40 (or_40_out, and_58_out, or_41_out);
  or or_41 (or_41_out, and_66_out, or_42_out);
  or or_42 (or_42_out, and_74_out, or_43_out);
  or or_43 (or_43_out, and_82_out, or_44_out);
  or or_44 (or_44_out, and_90_out, or_45_out);
  or or_45 (or_45_out, and_98_out, and_106_out);
  or or_46 (or_46_out, and_33_out, or_47_out);
  or or_47 (or_47_out, and_41_out, or_48_out);
  or or_48 (or_48_out, and_49_out, or_49_out);
  or or_49 (or_49_out, and_57_out, or_50_out);
  or or_50 (or_50_out, and_65_out, or_51_out);
  or or_51 (or_51_out, and_73_out, or_52_out);
  or or_52 (or_52_out, and_81_out, or_53_out);
  or or_53 (or_53_out, and_89_out, or_54_out);
  or or_54 (or_54_out, and_97_out, and_105_out);
  or or_55 (or_55_out, and_32_out, or_56_out);
  or or_56 (or_56_out, and_40_out, or_57_out);
  or or_57 (or_57_out, and_48_out, or_58_out);
  or or_58 (or_58_out, and_56_out, or_59_out);
  or or_59 (or_59_out, and_64_out, or_60_out);
  or or_60 (or_60_out, and_72_out, or_61_out);
  or or_61 (or_61_out, and_80_out, or_62_out);
  or or_62 (or_62_out, and_88_out, or_63_out);
  or or_63 (or_63_out, and_96_out, and_104_out);
  or or_64 (or_64_out, and_31_out, or_65_out);
  or or_65 (or_65_out, and_39_out, or_66_out);
  or or_66 (or_66_out, and_47_out, or_67_out);
  or or_67 (or_67_out, and_55_out, or_68_out);
  or or_68 (or_68_out, and_63_out, or_69_out);
  or or_69 (or_69_out, and_71_out, or_70_out);
  or or_70 (or_70_out, and_79_out, or_71_out);
  or or_71 (or_71_out, and_87_out, or_72_out);
  or or_72 (or_72_out, and_95_out, and_103_out);
endmodule
