// Logisim project step selector.circ as structural Verilog: 1 circuit, main circuit main
module main (
  input  [5:0] in_1,
  input  in_2,
  input  [5:0] in_3,
  output [5:0] out_4
);

  wire and_1_out, and_2_out, and_3_out, and_4_out, and_5_out, and_6_out, and_7_out, and_8_out, and_9_out,
       and_10_out, and_11_out, and_12_out, not_1_out;

  not not_1 (not_1_out, in_2);
  and and_1 (and_1_out, in_1[5], not_1_out);
  and and_2 (and_2_out, in_2, in_3[5]);
  or or_1 (out_4[5], and_1_out, and_2_out);
  and and_3 (and_3_out, in_1[4], not_1_out);
  and and_4 (and_4_out, in_2, in_3[4]);
  and and_5 (and_5_out, in_1[3], not_1_out);
  or or_2 (out_4[4], and_3_out, and_4_out);
  and and_6 (and_6_out, in_2, in_3[3]);
  and and_7 (and_7_out, in_1[2], not_1_out);
  or or_3 (out_4[3], and_5_out, and_6_out);
  and and_8 (and_8_out, in_2, in_3[2]);
  and and_9 (and_9_out, in_1[1], not_1_out);
  or or_4 (out_4[2], and_7_out, and_8_out);
  and and_10 (and_10_out, in_2, in_3[1]);
  and and_11 (and_11_out, in_1[0], not_1_out);
  or or_5 (out_4[1], and_9_out, and_10_out);
  and and_12 (and_12_out, in_2, in_3[0]);
  or or_6 (out_4[0], and_11_out, and_12_out);
endmodule
