// Logisim project subtraction using 2s compliment.circ as structural Verilog: 1 circuit, main circuit main
module main (
  input  in_1,
  input  in_2,
  input  in_3,
  input  in_4,
  input  in_5,
  input  in_6,
  input  in_7,
  input  in_8,
  input  in_9,
  input  in_10,
  input  in_11,
  input  in_12,
  output out_13,
  output out_14,
  output out_15,
  output out_16,
  output out_17,
  output out_18
);

  wire and_1_out, and_2_out, and_3_out, and_4_out, and_5_out, and_6_out, and_7_out, and_8_out, and_9_out,
       and_10_out, and_11_out, and_12_out, and_13_out, and_14_out, and_15_out, not_1_out, not_2_out,
       not_3_out, not_4_out, not_5_out, not_6_out, or_1_out, or_2_out, or_3_out, or_4_out, or_5_out,
       xor_1_out, xor_2_out, xor_3_out, xor_4_out, xor_5_out, xor_6_out, xor_7_out, xor_8_out, xor_9_out,
       xor_10_out, xor_11_out, xor_12_out;

  not not_1 (not_1_out, in_7);
  not not_2 (not_2_out, in_10);
  not not_3 (not_3_out, in_9);
  not not_4 (not_4_out, in_8);
  not not_5 (not_5_out, in_12);
  not not_6 (not_6_out, in_11);
  xor xor_1 (xor_1_out, 1'b1, not_5_out);
  and and_1 (and_1_out, 1'b1, not_5_out);
  xor xor_2 (xor_2_out, and_1_out, not_6_out);
  and and_2 (and_2_out, and_1_out, not_6_out);
  xor xor_3 (xor_3_out, and_2_out, not_2_out);
  and and_3 (and_3_out, and_2_out, not_2_out);
  xor xor_4 (xor_4_out, and_3_out, not_3_out);
  and and_4 (and_4_out, and_3_out, not_3_out);
  xor xor_5 (xor_5_out, and_4_out, not_4_out);
  and and_5 (and_5_out, and_4_out, not_4_out);
  xor xor_6 (xor_6_out, and_5_out, not_1_out);
  xor xor_7 (xor_7_out, xor_1_out, in_6);
  and and_6 (and_6_out, xor_1_out, in_6);
  xor xor_8 (xor_8_out, xor_2_out, in_5);
  and and_7 (and_7_out, xor_2_out, in_5);
  xor xor_9 (xor_9_out, xor_3_out, in_4);
  and and_8 (and_8_out, xor_3_out, in_4);
  xor xor_10 (xor_10_out, xor_4_out, in_3);
  and and_9 (and_9_out, xor_4_out, in_3);
  xor xor_11 (xor_11_out, xor_5_out, in_2);
  and and_10 (and_10_out, xor_5_out, in_2);
  xor xor_12 (xor_12_out, xor_6_out, in_1);
  xor xor_13 (out_18, 1'b0, xor_7_out);
  and and_11 (and_11_out, 1'b0, xor_7_out);
  xor xor_14 (out_17, or_1_out, xor_8_out);
  and and_12 (and_12_out, or_1_out, xor_8_out);
  xor xor_15 (out_16, or_2_out, xor_9_out);
  and and_13 (and_13_out, or_2_out, xor_9_out);
  xor xor_16 (out_15, or_3_out, xor_10_out);
  and and_14 (and_14_out, or_3_out, xor_10_out);
  xor xor_17 (out_14, or_4_out, xor_11_out);
  and and_15 (and_15_out, or_4_out, xor_11_out);
  xor xor_18 (out_13, or_5_out, xor_12_out);
  or or_1 (or_1_out, and_11_out, and_6_out);
  or or_2 (or_2_out, and_12_out, and_7_out);
  or or_3 (or_3_out, and_13_out, and_8_out);
  or or_4 (or_4_out, and_14_out, and_9_out);
  or or_5 (or_5_out, and_15_out, and_10_out);
endmodule
