// Logisim project subtraction2.circ as structural Verilog: 1 circuit, main circuit main
module main (
  input  in_1,
  input  in_2,
  input  in_3,
  input  in_4,
  input  in_5,
  input  in_6,
  input  in_7,
  input  in_8,
  input  in_9,
  input  in_10,
  input  in_11,
  input  in_12
);

  wire and_1_out, and_2_out, and_3_out, and_4_out, and_5_out, and_6_out, and_7_out, and_8_out, and_9_out,
       and_10_out, and_11_out, and_12_out, and_13_out, and_14_out, and_15_out, xor_1_out, xor_2_out,
       xor_3_out, xor_4_out, xor_5_out, xor_6_out, xor_7_out, xor_8_out, xor_9_out, xor_10_out, xor_11_out,
       xor_12_out, xor_13_out, xor_14_out, xor_15_out, xor_16_out, xor_17_out, xor_18_out, xor_19_out,
       xor_20_out, xor_21_out;

  LED led_1 (.in(xor_1_out));
  LED led_2 (.in(xor_2_out));
  LED led_3 (.in(xor_3_out));
  LED led_4 (.in(xor_4_out));
  LED led_5 (.in(xor_5_out));
  LED led_6 (.in(xor_9_out));
  and and_1 (and_1_out, and_5_out, xor_10_out);
  xor xor_1 (xor_1_out, in_1, and_1_out);
  and and_2 (and_2_out, and_6_out, xor_6_out);
  xor xor_2 (xor_2_out, xor_1_out, and_2_out);
  and and_3 (and_3_out, and_7_out, xor_7_out);
  xor xor_3 (xor_3_out, xor_2_out, and_3_out);
  and and_4 (and_4_out, and_12_out, xor_8_out);
  xor xor_4 (xor_4_out, xor_3_out, and_4_out);
  xor xor_5 (xor_5_out, xor_4_out, and_9_out);
  LED led_7 (.in(xor_10_out));
  xor xor_6 (xor_6_out, xor_10_out, and_6_out);
  LED led_8 (.in(xor_6_out));
  xor xor_7 (xor_7_out, xor_6_out, and_7_out);
  LED led_9 (.in(xor_7_out));
  xor xor_8 (xor_8_out, xor_7_out, and_12_out);
  LED led_10 (.in(xor_8_out));
  LED led_11 (.in(xor_11_out));
  xor xor_9 (xor_9_out, xor_5_out, in_7);
  and and_5 (and_5_out, and_10_out, xor_12_out);
  xor xor_10 (xor_10_out, in_2, and_5_out);
  and and_6 (and_6_out, and_8_out, xor_13_out);
  LED led_12 (.in(xor_13_out));
  and and_7 (and_7_out, and_13_out, xor_14_out);
  LED led_13 (.in(xor_14_out));
  LED led_14 (.in(xor_16_out));
  xor xor_11 (xor_11_out, xor_8_out, in_8);
  xor xor_12 (xor_12_out, in_3, and_10_out);
  LED led_15 (.in(xor_12_out));
  and and_8 (and_8_out, and_14_out, xor_15_out);
  xor xor_13 (xor_13_out, xor_12_out, and_8_out);
  xor xor_14 (xor_14_out, xor_13_out, and_13_out);
  and and_9 (and_9_out, xor_11_out, in_8);
  and and_10 (and_10_out, and_11_out, xor_17_out);
  LED led_16 (.in(xor_17_out));
  xor xor_15 (xor_15_out, xor_17_out, and_14_out);
  LED led_17 (.in(xor_15_out));
  LED led_18 (.in(xor_18_out));
  xor xor_16 (xor_16_out, xor_14_out, in_9);
  and and_11 (and_11_out, and_15_out, xor_19_out);
  xor xor_17 (xor_17_out, in_4, and_11_out);
  LED led_19 (.in(xor_20_out));
  xor xor_18 (xor_18_out, xor_15_out, in_10);
  and and_12 (and_12_out, xor_16_out, in_9);
  xor xor_19 (xor_19_out, in_5, and_15_out);
  LED led_20 (.in(xor_19_out));
  LED led_21 (.in(xor_21_out));
  and and_13 (and_13_out, xor_18_out, in_10);
  xor xor_20 (xor_20_out, xor_19_out, in_11);
  xor xor_21 (xor_21_out, in_6, in_12);
  and and_14 (and_14_out, xor_20_out, in_11);
  and and_15 (and_15_out, xor_21_out, in_12);
  LED led_22 (.in(xor_9_out));
  LED led_23 (.in(xor_11_out));
  LED led_24 (.in(xor_16_out));
  LED led_25 (.in(xor_21_out));
  LED led_26 (.in(xor_20_out));
  LED led_27 (.in(xor_18_out));
endmodule
