// Logisim project value transfer.circ as structural Verilog: 1 circuit, main circuit main
module main (
  input  [5:0] Inp_A,
  input  [5:0] Inp_C,
  input  [5:0] Inp_B,
  output [5:0] To_B,
  output [5:0] To_A,
  output [5:0] To_C
);

  or or_1 (To_B[5], Inp_A[5], Inp_C[5]);
  or or_2 (To_B[4], Inp_A[4], Inp_C[4]);
  or or_3 (To_B[3], Inp_A[3], Inp_C[3]);
  or or_4 (To_B[2], Inp_A[2], Inp_C[2]);
  or or_5 (To_B[1], Inp_A[1], Inp_C[1]);
  or or_6 (To_B[0], Inp_A[0], Inp_C[0]);
  or or_7 (To_A[5], Inp_C[5], Inp_B[5]);
  or or_8 (To_A[4], Inp_C[4], Inp_B[4]);
  or or_9 (To_A[3], Inp_C[3], Inp_B[3]);
  or or_10 (To_A[2], Inp_C[2], Inp_B[2]);
  or or_11 (To_A[1], Inp_C[1], Inp_B[1]);
  or or_12 (To_A[0], Inp_C[0], Inp_B[0]);
  or or_13 (To_C[5], Inp_B[5], Inp_A[5]);
  or or_14 (To_C[4], Inp_B[4], Inp_A[4]);
  or or_15 (To_C[3], Inp_B[3], Inp_A[3]);
  or or_16 (To_C[2], Inp_B[2], Inp_A[2]);
  or or_17 (To_C[1], Inp_B[1], Inp_A[1]);
  or or_18 (To_C[0], Inp_B[0], Inp_A[0]);
endmodule
